// Logisim project computer.circ as structural Verilog: 6 circuits, main circuit main
module main (
);

  wire addr_decoder_1_dma, addr_decoder_1_mem, addr_decoder_1_pia, bus_status_1_hldaout, bus_status_1_hrqout,
       bus_status_1_rwout, clock_1_out, cpu_single_cycle_1_hlda, cpu_single_cycle_1_rw, dmac_1_dclk,
       dmac_1_hrq, RST_out, tty_adapter_1_clk;
  wire [1:0] bus_status_1_alignout, cpu_single_cycle_1_dataalign;
  wire [6:0] keyboard_1_data, tty_adapter_1_data;
  wire [7:0] dmac_1_memdataout, io_status_1_dmadata, io_status_1_indipai, io_status_1_indipao,
       io_status_1_indipbi, io_status_1_indipbo, io_status_1_indipci, io_status_1_indipco, io_status_1_opai,
       io_status_1_opbi, io_status_1_opci, io_status_1_pao, io_status_1_pbo, io_status_1_pco, undriven,
       undriven_2, via_1_pao, via_1_pbo, via_1_pco;
  wire [7:7] keyboard_1_avail;
  wire [31:0] bus_status_1_oaddr, bus_status_1_odatain, bus_status_1_odataout, cpu_single_cycle_1_addr,
       cpu_single_cycle_1_dataout, memory_1_dataout;

  bus_status bus_status_1 (
    .AlignIn(cpu_single_cycle_1_dataalign), .RWIn(cpu_single_cycle_1_rw), .HRQIn(dmac_1_hrq),
    .HLDAIn(cpu_single_cycle_1_hlda), .iDataIn(memory_1_dataout), .iDataOut(cpu_single_cycle_1_dataout),
    .iAddr(cpu_single_cycle_1_addr), .oDataIn(bus_status_1_odatain), .oDataOut(bus_status_1_odataout),
    .AlignOut(bus_status_1_alignout), .RWOut(bus_status_1_rwout), .HRQOut(bus_status_1_hrqout),
    .HLDAOut(bus_status_1_hldaout), .oAddr(bus_status_1_oaddr));
  memory memory_1 (
    .Wr(cpu_single_cycle_1_rw), .En(addr_decoder_1_mem), .CLK(clock_1_out),
    .DataAlign(cpu_single_cycle_1_dataalign), .DataIn(cpu_single_cycle_1_dataout),
    .Addr(cpu_single_cycle_1_addr), .DataOut(memory_1_dataout));
  cpu_single_cycle cpu_single_cycle_1 (
    .RST(RST_out), .CLK(clock_1_out), .Hold(dmac_1_hrq), .DataIn(memory_1_dataout),
    .DataOut(cpu_single_cycle_1_dataout), .RW(cpu_single_cycle_1_rw),
    .DataAlign(cpu_single_cycle_1_dataalign), .HLDA(cpu_single_cycle_1_hlda), .Addr(cpu_single_cycle_1_addr));
  DotMatrix #(.dotshape("clusterSegment"), .inputtype("row"), .matrixcols(32), .matrixrows(1)) dotmatrix_1 (.row0(bus_status_1_oaddr));
  DotMatrix #(.dotshape("clusterSegment"), .inputtype("row"), .matrixcols(32), .matrixrows(1)) dotmatrix_2 (.row0(bus_status_1_odatain));
  DotMatrix #(.dotshape("clusterSegment"), .inputtype("row"), .matrixcols(32), .matrixrows(1)) dotmatrix_3 (.row0(bus_status_1_odataout));
  DotMatrix #(.dotshape("clusterSegment"), .inputtype("row"), .matrixcols(2), .matrixrows(1)) dotmatrix_4 (.row0(bus_status_1_alignout));
  DotMatrix #(.dotshape("clusterSegment"), .inputtype("row"), .matrixcols(1), .matrixrows(1)) dotmatrix_5 (.row0(bus_status_1_rwout));
  DotMatrix #(.dotshape("clusterSegment"), .inputtype("row"), .matrixcols(1), .matrixrows(1)) dotmatrix_6 (.row0(bus_status_1_hrqout));
  DotMatrix #(.dotshape("clusterSegment"), .inputtype("row"), .matrixcols(1), .matrixrows(1)) dotmatrix_7 (.row0(bus_status_1_hldaout));
  dmac dmac_1 (
    .En(addr_decoder_1_dma), .We(cpu_single_cycle_1_rw), .CLK(clock_1_out), .RST(RST_out),
    .HLDA(cpu_single_cycle_1_hlda), .Rs(cpu_single_cycle_1_addr), .DataIn(cpu_single_cycle_1_dataout),
    .MemDataIn(memory_1_dataout), .MemAddr(cpu_single_cycle_1_addr), .MemDataOut(dmac_1_memdataout),
    .HRQ(dmac_1_hrq), .DCLK(dmac_1_dclk));
  addr_decoder addr_decoder_1 (
    .Addr(cpu_single_cycle_1_addr), .DMA(addr_decoder_1_dma), .MEM(addr_decoder_1_mem),
    .PIA(addr_decoder_1_pia));
  via via_1 (
    .PBI(io_status_1_opbi), .PAI(io_status_1_opai), .PCI(io_status_1_opci), .En(addr_decoder_1_pia),
    .RW(cpu_single_cycle_1_rw), .CLK(clock_1_out), .RST(RST_out), .Rs(cpu_single_cycle_1_addr),
    .DataIn(cpu_single_cycle_1_dataout), .PAO(via_1_pao), .PBO(via_1_pbo), .DataOut(memory_1_dataout),
    .PCO(via_1_pco));
  Clock clock_1 (.out(clock_1_out));
  Button RST (.out(RST_out));
  io_status io_status_1 (
    .PAI(undriven), .PBI({keyboard_1_avail[7], keyboard_1_data}), .PCI(undriven_2), .iPAO(via_1_pao),
    .iPBO(via_1_pbo), .iPCO(via_1_pco), .iDMAData(dmac_1_memdataout), .oPAI(io_status_1_opai),
    .oPBI(io_status_1_opbi), .oPCI(io_status_1_opci), .PAO(io_status_1_pao), .PBO(io_status_1_pbo),
    .PCO(io_status_1_pco), .DMAData(io_status_1_dmadata), .IndiPAI(io_status_1_indipai),
    .IndiPBI(io_status_1_indipbi), .IndiPCI(io_status_1_indipci), .IndiPAO(io_status_1_indipao),
    .indiPBO(io_status_1_indipbo), .indiPCO(io_status_1_indipco));
  DotMatrix #(.dotshape("clusterSegment"), .inputtype("row"), .matrixcols(8), .matrixrows(1)) dotmatrix_8 (.row0(io_status_1_indipao));
  DotMatrix #(.dotshape("clusterSegment"), .inputtype("row"), .matrixcols(8), .matrixrows(1)) dotmatrix_9 (.row0(io_status_1_indipbo));
  DotMatrix #(.dotshape("clusterSegment"), .inputtype("row"), .matrixcols(8), .matrixrows(1)) dotmatrix_10 (.row0(io_status_1_indipco));
  DotMatrix #(.dotshape("clusterSegment"), .inputtype("row"), .matrixcols(8), .matrixrows(1)) dotmatrix_11 (.row0(io_status_1_indipai));
  DotMatrix #(.dotshape("clusterSegment"), .inputtype("row"), .matrixcols(8), .matrixrows(1)) dotmatrix_12 (.row0(io_status_1_indipbi));
  DotMatrix #(.dotshape("clusterSegment"), .inputtype("row"), .matrixcols(8), .matrixrows(1)) dotmatrix_13 (.row0(io_status_1_indipci));
  DotMatrix #(.dotshape("clusterSegment"), .inputtype("row"), .matrixcols(8), .matrixrows(1)) dotmatrix_14 (.row0(io_status_1_dmadata));
  tty_adapter tty_adapter_1 (
    .Mode(io_status_1_pco[1]), .DMACLK(dmac_1_dclk), .PIAData(io_status_1_pao), .DMAData(dmac_1_memdataout),
    .Data(tty_adapter_1_data), .CLK(tty_adapter_1_clk));
  TTY #(.cols(40), .rows(10)) tty_1 (.data(tty_adapter_1_data), .clk(tty_adapter_1_clk), .clr(RST_out));  // open: we
  Keyboard #(.buflen(80)) keyboard_1 (
    .clk(io_status_1_pco[0]), .clr(RST_out), .avail(keyboard_1_avail[7]), .data(keyboard_1_data));  // open: re

  // Notes on the sheet:
  //   Type Here
endmodule

module memory (
  input  [31:0] Addr,
  input  Wr,
  input  En,
  input  [1:0] DataAlign,
  input  CLK,
  input  [31:0] DataIn,
  output [31:0] DataOut
);

  wire and_1_out, ram_1_p4;
  wire [7:0] ram_1_p12, ram_1_p13, ram_1_p14, ram_1_p15;
  wire [15:0] bit_extender_1_out;

  Bit_Extender #(.in_width(32), .\type ("zero")) bit_extender_1 (.in(Addr), .out(bit_extender_1_out));
  and and_1 (and_1_out, Wr, En);
  // RAM #(.addrWidth(16), .enables("line"), .line("quad"), .misaligned("true"), .trigger("falling"), .\type ("nonvolatile")) ram_1: pin names not known; wires that end beside it: bit_extender_1_out, and_1_out, 1'b1, ram_1_p4, DataAlign[1], DataAlign[1], CLK, DataIn[7:0], DataIn[15:8], DataIn[23:16], DataIn[31:24], ram_1_p12, ram_1_p13, ram_1_p14, ram_1_p15
  or or_1 (ram_1_p4, DataAlign[0], DataAlign[1]);
  assign DataOut = En ? {ram_1_p15, ram_1_p14, ram_1_p13, ram_1_p12} : 32'bz;  // Controlled_Buffer controlled_buffer_1
endmodule

module addr_decoder (
  input  [31:0] Addr,
  output DMA,
  output MEM,
  output PIA
);

  wire comparator_1_eq, comparator_1_gt, comparator_2_eq, comparator_2_lt, comparator_3_eq, comparator_3_gt,
       comparator_4_eq, comparator_4_lt, or_1_out, or_2_out, or_3_out, or_4_out;
  wire [15:0] bit_extender_1_out;

  Bit_Extender #(.in_width(32), .\type ("zero")) bit_extender_1 (.in(Addr), .out(bit_extender_1_out));
  Comparator #(.mode("unsigned"), .width(16)) comparator_1 (
    .a(bit_extender_1_out), .b(16'hfff8), .gt(comparator_1_gt), .eq(comparator_1_eq));  // open: lt
  Comparator #(.mode("unsigned"), .width(16)) comparator_2 (
    .a(bit_extender_1_out), .b({16{1'b1}}), .eq(comparator_2_eq), .lt(comparator_2_lt));  // open: gt
  Comparator #(.mode("unsigned"), .width(16)) comparator_3 (
    .a(bit_extender_1_out), .b(16'hfff4), .gt(comparator_3_gt), .eq(comparator_3_eq));  // open: lt
  Comparator #(.mode("unsigned"), .width(16)) comparator_4 (
    .a(bit_extender_1_out), .b(16'hfff7), .eq(comparator_4_eq), .lt(comparator_4_lt));  // open: gt
  or or_1 (or_1_out, comparator_4_lt, comparator_4_eq);
  or or_2 (or_2_out, comparator_3_eq, comparator_3_gt);
  and and_1 (DMA, or_1_out, or_2_out);
  nor nor_1 (MEM, DMA, PIA);
  or or_3 (or_3_out, comparator_2_lt, comparator_2_eq);
  or or_4 (or_4_out, comparator_1_eq, comparator_1_gt);
  and and_2 (PIA, or_3_out, or_4_out);
endmodule

module io_status (
  input  [7:0] PAI,
  input  [7:0] PBI,
  input  [7:0] PCI,
  input  [7:0] iPAO,
  input  [7:0] iPBO,
  input  [7:0] iPCO,
  input  [7:0] iDMAData,
  output [7:0] oPAI,
  output [7:0] oPBI,
  output [7:0] oPCI,
  output [7:0] PAO,
  output [7:0] PBO,
  output [7:0] PCO,
  output [7:0] DMAData,
  output [7:0] IndiPAI,
  output [7:0] IndiPBI,
  output [7:0] IndiPCI,
  output [7:0] IndiPAO,
  output [7:0] indiPBO,
  output [7:0] indiPCO
);


  assign DMAData = iDMAData;
  assign IndiPAI = PAI;
  assign IndiPAO = iPAO;
  assign IndiPBI = PBI;
  assign indiPBO = iPBO;
  assign IndiPCI = PCI;
  assign indiPCO = iPCO;
  assign oPAI = PAI;
  assign oPBI = PBI;
  assign oPCI = PCI;
  assign PAO = iPAO;
  assign PBO = iPBO;
  assign PCO = iPCO;
endmodule

module bus_status (
  input  [31:0] iAddr,
  input  [31:0] iDataIn,
  input  [31:0] iDataOut,
  input  [1:0] AlignIn,
  input  RWIn,
  input  HRQIn,
  input  HLDAIn,
  output [31:0] oAddr,
  output [31:0] oDataIn,
  output [31:0] oDataOut,
  output [1:0] AlignOut,
  output RWOut,
  output HRQOut,
  output HLDAOut
);


  assign AlignOut = AlignIn;
  assign HLDAOut = HLDAIn;
  assign HRQOut = HRQIn;
  assign oAddr = iAddr;
  assign oDataIn = iDataIn;
  assign oDataOut = iDataOut;
  assign RWOut = RWIn;
endmodule

module tty_adapter (
  input  [7:0] PIAData,
  input  [7:0] DMAData,
  input  Mode,
  input  DMACLK,
  output [6:0] Data,
  output CLK
);

  wire [7:7] multiplexer_1_out;

  Multiplexer #(.width(8)) multiplexer_1 (.in0(PIAData), .in1(DMAData), .out({multiplexer_1_out[7], Data}), .sel(Mode));
  Multiplexer multiplexer_2 (.in0(PIAData[7]), .in1(DMACLK), .out(CLK), .sel(Mode));
endmodule
