// Logisim project dma.circ as structural Verilog: 3 circuits, main circuit the_dma
module the_dma (
  input  [31:0] mdata,
  input  [31:0] cdata,
  input  en,
  input  wr,
  input  [31:0] rs,
  input  clk,
  input  rst,
  input  hlda,
  output [7:0] data,
  output [31:0] addr,
  output hld,
  output dclk
);

  wire and_1_out, and_2_out, and_3_out, comparator_1_eq, counter_2_carry, decoder_1_out0, decoder_1_out1,
       decoder_1_out2, not_1_out;
  wire [1:0] bit_extender_1_out;
  wire [7:0] bit_extender_2_out, bit_extender_3_out, bit_extender_4_out, bit_extender_5_out;
  wire [15:0] size_reg_1_size;
  wire [19:0] addr_reg_1_addr, counter_1_q;
  wire [31:0] bit_extender_6_out;

  Decoder #(.select(2)) decoder_1 (
    .out0(decoder_1_out0), .out1(decoder_1_out1), .out2(decoder_1_out2), .sel(bit_extender_1_out),
    .en(and_1_out));  // open: out3
  and and_1 (and_1_out, en, wr);
  Bit_Extender #(.in_width(32), .out_width(2), .\type ("zero")) bit_extender_1 (.in(rs), .out(bit_extender_1_out));
  not not_1 (not_1_out, clk);
  Bit_Extender #(.in_width(32), .out_width(8), .\type ("zero")) bit_extender_2 (.in(mdata), .out(bit_extender_2_out));
  Bit_Extender #(.in_width(32), .out_width(8), .\type ("zero")) bit_extender_3 (.in(cdata), .out(bit_extender_3_out));
  Bit_Extender #(.in_width(32), .out_width(8), .\type ("zero")) bit_extender_4 (.in(cdata), .out(bit_extender_4_out));
  Bit_Extender #(.in_width(32), .out_width(8), .\type ("zero")) bit_extender_5 (.in(cdata), .out(bit_extender_5_out));
  Comparator #(.mode("unsigned")) comparator_1 (
    .a(bit_extender_5_out), .b({8{1'b0}}), .eq(comparator_1_eq));  // open: gt, lt
  and and_2 (and_2_out, ~comparator_1_eq, decoder_1_out2);  // AND_Gate
  addr_reg addr_reg_1 (
    .addr(addr_reg_1_addr), .en(decoder_1_out0), .clk(not_1_out), .rst(rst), .data(bit_extender_3_out));
  size_reg size_reg_1 (
    .size(size_reg_1_size), .en(decoder_1_out1), .clk(not_1_out), .rst(rst), .data(bit_extender_4_out));
  S_R_Flip_Flop s_r_ff_1 (.S(and_2_out), .R(and_3_out), .clk(not_1_out), .Q(hld), .reset(rst));  // open: Qn, preset
  and and_3 (and_3_out, hld, counter_2_carry);
  Pull_Resistor pull_resistor_1 (.node(data));
  assign data = hlda ? bit_extender_2_out : 8'bz;  // Controlled_Buffer controlled_buffer_1
  Counter #(.max('hfffff), .width(20)) counter_1 (
    .load(and_2_out), .D(addr_reg_1_addr), .count(hlda), .Q(counter_1_q), .clk(not_1_out), .clr(rst));  // open: carry, up
  Counter #(.max('hffff), .ongoal("stay"), .width(16)) counter_2 (
    .load(and_2_out), .D(size_reg_1_size), .count(hlda), .carry(counter_2_carry), .up(1'b0), .clk(not_1_out),
    .clr(rst));  // open: Q
  assign bit_extender_6_out = {{12{1'b0}}, counter_1_q};  // Bit_Extender bit_extender_6
  assign addr = hlda ? bit_extender_6_out : 32'bz;  // Controlled_Buffer controlled_buffer_2
  and and_4 (dclk, not_1_out, hlda);
endmodule

module addr_reg (
  input  [7:0] data,
  input  en,
  input  clk,
  input  rst,
  output [19:0] addr
);

  wire decoder_1_out0, decoder_1_out1, decoder_1_out2;
  wire [1:0] counter_1_q;
  wire [7:4] register_3_q;

  Counter #(.max('h2), .width(2)) counter_1 (
    .count(en), .Q(counter_1_q), .clk(clk), .clr(rst));  // open: load, D, carry, up
  Decoder #(.select(2)) decoder_1 (
    .out0(decoder_1_out0), .out1(decoder_1_out1), .out2(decoder_1_out2), .sel(counter_1_q), .en(en));  // open: out3
  Register register_1 (.D(data), .en(decoder_1_out0), .Q(addr[7:0]), .clk(clk), .clr(rst));
  Register register_2 (.D(data), .en(decoder_1_out1), .Q(addr[15:8]), .clk(clk), .clr(rst));
  Register register_3 (.D(data), .en(decoder_1_out2), .Q({register_3_q, addr[19:16]}), .clk(clk), .clr(rst));
endmodule

module size_reg (
  input  [7:0] data,
  input  en,
  input  clk,
  input  rst,
  output [15:0] size
);

  wire counter_1_q, decoder_1_out0, decoder_1_out1;

  Counter #(.max('h1), .width(1)) counter_1 (
    .count(en), .Q(counter_1_q), .clk(clk), .clr(rst));  // open: load, D, carry, up
  Decoder decoder_1 (.out0(decoder_1_out0), .out1(decoder_1_out1), .sel(counter_1_q), .en(en));
  Register register_1 (.D(data), .en(decoder_1_out0), .Q(size[7:0]), .clk(clk), .clr(rst));
  Register register_2 (.D(data), .en(decoder_1_out1), .Q(size[15:8]), .clk(clk), .clr(rst));
endmodule
