// Logisim project dmac.circ as structural Verilog: 2 circuits, main circuit dmac
module dmac (
  input  [31:0] MemDataIn,
  input  [31:0] DataIn,
  input  En,
  input  We,
  input  [31:0] Rs,
  input  CLK,
  input  RST,
  input  HLDA,
  output [7:0] MemDataOut,
  output [31:0] MemAddr,
  output HRQ,
  output DCLK
);

  wire and_1_out, and_2_out, and_3_out, counter_2_carry, decoder_1_out0, decoder_1_out1, decoder_1_out2,
       decoder_1_out3, not_1_out;
  wire [1:0] bit_extender_1_out;
  wire [7:0] bit_extender_2_out, bit_extender_3_out;
  wire [15:0] Block_Address_dataout, Block_Size_dataout, counter_1_q;
  wire [31:0] bit_extender_4_out;

  Decoder #(.select(2)) decoder_1 (
    .out0(decoder_1_out0), .out1(decoder_1_out1), .out2(decoder_1_out2), .out3(decoder_1_out3),
    .sel(bit_extender_1_out), .en(and_1_out));
  and and_1 (and_1_out, En, We);
  Bit_Extender #(.in_width(32), .out_width(2), .\type ("zero")) bit_extender_1 (.in(Rs), .out(bit_extender_1_out));
  not not_1 (not_1_out, CLK);
  Bit_Extender #(.in_width(32), .out_width(8), .\type ("zero")) bit_extender_2 (
    .in(MemDataIn), .out(bit_extender_2_out));
  Bit_Extender #(.in_width(32), .out_width(8), .\type ("zero")) bit_extender_3 (.in(DataIn), .out(bit_extender_3_out));
  S_R_Flip_Flop s_r_ff_1 (
    .S(decoder_1_out1), .R(and_2_out), .clk(not_1_out), .Q(HRQ), .reset(RST));  // open: Qn, preset
  and and_2 (and_2_out, HRQ, counter_2_carry);
  dmac_reg Block_Address (
    .LoEn(decoder_1_out0), .HiEn(decoder_1_out1), .CLK(not_1_out), .RST(RST), .DataLo(bit_extender_3_out),
    .DataOut(Block_Address_dataout));
  dmac_reg Block_Size (
    .LoEn(decoder_1_out2), .HiEn(decoder_1_out3), .CLK(not_1_out), .RST(RST), .DataLo(bit_extender_3_out),
    .DataOut(Block_Size_dataout));
  assign MemDataOut = and_3_out ? bit_extender_2_out : 8'bz;  // Controlled_Buffer controlled_buffer_1
  and and_3 (and_3_out, HRQ, HLDA);
  Counter #(.max('hffff), .trigger("falling"), .width(16)) counter_1 (
    .load(decoder_1_out1), .D(Block_Address_dataout), .count(and_3_out), .Q(counter_1_q), .clk(not_1_out),
    .clr(RST));  // open: carry, up
  Counter #(.max('hffff), .ongoal("stay"), .trigger("falling"), .width(16)) counter_2 (
    .load(decoder_1_out1), .D(Block_Size_dataout), .count(and_3_out), .carry(counter_2_carry), .up(1'b0),
    .clk(not_1_out), .clr(RST));  // open: Q
  assign bit_extender_4_out = {{16{1'b0}}, counter_1_q};  // Bit_Extender bit_extender_4
  assign MemAddr = and_3_out ? bit_extender_4_out : 32'bz;  // Controlled_Buffer controlled_buffer_2
  and and_4 (DCLK, not_1_out, HLDA);
endmodule

module dmac_reg (
  input  [7:0] DataLo,
  input  LoEn,
  input  HiEn,
  input  CLK,
  input  RST,
  output [15:0] DataOut
);

  Register register_1 (.D(DataLo), .en(LoEn), .Q(DataOut[7:0]), .clk(CLK), .clr(RST));
  Register register_2 (.D(DataLo), .en(HiEn), .Q(DataOut[15:8]), .clk(CLK), .clr(RST));
endmodule
