// Logisim project pia.circ as structural Verilog: 6 circuits, main circuit pia
module pia (
  input  [31:0] data_in,
  input  [7:0] pra_in,
  input  [7:0] prb_in,
  input  en,
  input  wr,
  input  [31:0] rs,
  input  rd,
  input  clk,
  input  rst,
  output [7:0] pra_out,
  output [7:0] prb_out,
  output [31:0] data_out,
  output io_wr,
  output io_rd
);

  wire and_1_out, and_3_out, and_4_out, and_5_out, decoder_1_out0, decoder_1_out1, decoder_1_out2,
       decoder_1_out3, decoder_1_out4, decoder_1_out5, decoder_1_out6, nor_1_out, not_1_out, or_1_out;
  wire [2:0] bit_extender_1_out;
  wire [7:0] bit_extender_2_out, controlled_buffer_1_out, io_port_1_ddr, io_port_1_port_data, io_port_2_ddr,
       io_port_2_port_data, multiplexer_1_out, register_1_q, timer_1_cnt_val, timer_1_ctrl_val, timer_1_fl;

  and and_1 (and_1_out, en, wr);
  Bit_Extender #(.in_width(32), .out_width(3), .\type ("zero")) bit_extender_1 (.in(rs), .out(bit_extender_1_out));
  and and_2 (io_rd, en, rd);
  not not_1 (not_1_out, clk);
  Decoder #(.select(3)) decoder_1 (
    .out0(decoder_1_out0), .out1(decoder_1_out1), .out2(decoder_1_out2), .out3(decoder_1_out3),
    .out4(decoder_1_out4), .out5(decoder_1_out5), .out6(decoder_1_out6), .sel(bit_extender_1_out),
    .en(and_1_out));  // open: out7
  Bit_Extender #(.in_width(32), .out_width(8), .\type ("zero")) bit_extender_2 (.in(data_in), .out(bit_extender_2_out));
  nor nor_1 (nor_1_out, bit_extender_1_out[0], bit_extender_1_out[1], bit_extender_1_out[2]);
  and and_3 (and_3_out, ~bit_extender_1_out[0], bit_extender_1_out[1], ~bit_extender_1_out[2]);  // AND_Gate
  and and_4 (and_4_out, bit_extender_1_out[2], bit_extender_1_out[1], bit_extender_1_out[0]);
  or or_1 (or_1_out, nor_1_out, and_3_out);
  and and_5 (and_5_out, and_4_out, io_rd);
  io_port io_port_1 (
    .ddr(io_port_1_ddr), .write_port(pra_out), .port_data(io_port_1_port_data), .pr_ld(decoder_1_out0),
    .ddr_ld(decoder_1_out1), .clk(not_1_out), .rst(rst), .data_in(bit_extender_2_out), .read_port(pra_in));
  io_port io_port_2 (
    .ddr(io_port_2_ddr), .write_port(prb_out), .port_data(io_port_2_port_data), .pr_ld(decoder_1_out2),
    .ddr_ld(decoder_1_out3), .clk(not_1_out), .rst(rst), .data_in(bit_extender_2_out), .read_port(prb_in));
  timer timer_1 (
    .fl(timer_1_fl), .ctrl_val(timer_1_ctrl_val), .cnt_val(timer_1_cnt_val), .cnt_ld(decoder_1_out4),
    .cmp_ld(decoder_1_out5), .ctrl_ld(decoder_1_out6), .rd_fl(and_5_out), .clk(not_1_out), .rst(rst),
    .data(bit_extender_2_out));
  Multiplexer #(.select(3), .width(8)) multiplexer_1 (
    .in0(io_port_1_port_data), .in1(io_port_1_ddr), .in2(io_port_2_port_data), .in3(io_port_2_ddr),
    .in4(timer_1_cnt_val), .in6(timer_1_ctrl_val), .in7(timer_1_fl), .out(multiplexer_1_out),
    .sel(bit_extender_1_out));  // open: in5
  and and_6 (io_wr, or_1_out, and_1_out);
  assign controlled_buffer_1_out = io_rd ? register_1_q : 8'bz;  // Controlled_Buffer controlled_buffer_1
  Register register_1 (.D(multiplexer_1_out), .Q(register_1_q), .clk(io_rd), .clr(rst));  // open: en
  assign data_out = {{24{controlled_buffer_1_out[7]}}, controlled_buffer_1_out};  // Bit_Extender bit_extender_3
endmodule

module io_port (
  input  [7:0] data_in,
  input  pr_ld,
  input  ddr_ld,
  input  [7:0] read_port,
  input  clk,
  input  rst,
  output [7:0] ddr,
  output [7:0] write_port,
  output [7:0] port_data
);

  wire [7:0] not_1_out, register_2_q;

  Register register_1 (.D(data_in), .en(pr_ld), .Q(ddr), .clk(clk), .clr(rst));
  Register register_2 (.D(data_in), .en(ddr_ld), .Q(register_2_q), .clk(clk), .clr(rst));
  assign not_1_out = ~ddr;  // NOT_Gate not_1, 8 bits wide
  buff8 buff8_1 (.data_out(port_data), .data_in(read_port), .en(not_1_out));
  buff8 buff8_2 (.data_out(write_port), .data_in(register_2_q), .en(ddr));
  Pull_Resistor pull_resistor_1 (.node(port_data));
  Pull_Resistor pull_resistor_2 (.node(write_port));
endmodule

module timer (
  input  cnt_ld,
  input  [7:0] data,
  input  cmp_ld,
  input  ctrl_ld,
  input  rd_fl,
  input  clk,
  input  rst,
  output [7:0] cnt_val,
  output [7:0] fl,
  output [7:0] ctrl_val
);

  wire and_1_out, and_2_out, and_3_out, compare_1_eq, d_ff_1_q, d_ff_2_q, multiplexer_1_out, not_1_out,
       or_1_out, prescaler_1_clk_out, s_r_ff_1_q;
  wire [7:0] cmp_q;

  Register ctrl (.D(data), .en(ctrl_ld), .Q(ctrl_val), .clk(clk), .clr(rst));
  prescaler prescaler_1 (.clk_out(prescaler_1_clk_out), .en(ctrl_val[0]), .clk(clk), .rst(rst), .freq_sel(ctrl_val));
  not not_1 (not_1_out, ctrl_val[1]);
  and and_1 (and_1_out, cnt_ld, not_1_out);
  Multiplexer multiplexer_1 (.in0(prescaler_1_clk_out), .in1(clk), .out(multiplexer_1_out), .sel(and_1_out));
  Counter cnt (
    .load(and_1_out), .D(data), .count(ctrl_val[0]), .Q(cnt_val), .clk(multiplexer_1_out), .clr(or_1_out));  // open: carry, up
  or or_1 (or_1_out, rst, and_2_out);
  and and_2 (and_2_out, ctrl_val[1], d_ff_2_q);
  Register cmp (.D(data), .en(cmp_ld), .Q(cmp_q), .clk(clk), .clr(rst));
  D_Flip_Flop d_ff_1 (.D(rd_fl), .clk(clk), .Q(d_ff_1_q), .reset(rst));  // open: Qn, preset
  compare compare_1 (.eq(compare_1_eq), .en(not_1_out), .a(cnt_val), .b({8{1'b0}}));
  compare compare_2 (.eq(compare_1_eq), .en(ctrl_val[1]), .a(cnt_val), .b(cmp_q));
  Pull_Resistor pull_resistor_1 (.node(compare_1_eq));
  D_Flip_Flop d_ff_2 (.D(and_3_out), .clk(clk), .Q(d_ff_2_q), .reset(rst));  // open: Qn, preset
  and and_3 (and_3_out, compare_1_eq, ctrl_val[0]);
  S_R_Flip_Flop s_r_ff_1 (
    .S(1'b0), .R(d_ff_1_q), .clk(clk), .Q(s_r_ff_1_q), .reset(rst), .preset(d_ff_2_q));  // open: Qn
  assign fl = {{7{s_r_ff_1_q}}, s_r_ff_1_q};  // Bit_Extender bit_extender_1
endmodule

module buff8 (
  input  [7:0] data_in,
  input  [7:0] en,
  output [7:0] data_out
);

  assign data_out[0] = en[0] ? data_in[0] : 1'bz;  // Controlled_Buffer controlled_buffer_1
  assign data_out[1] = en[1] ? data_in[1] : 1'bz;  // Controlled_Buffer controlled_buffer_2
  assign data_out[2] = en[2] ? data_in[2] : 1'bz;  // Controlled_Buffer controlled_buffer_3
  assign data_out[3] = en[3] ? data_in[3] : 1'bz;  // Controlled_Buffer controlled_buffer_4
  assign data_out[4] = en[4] ? data_in[4] : 1'bz;  // Controlled_Buffer controlled_buffer_5
  assign data_out[5] = en[5] ? data_in[5] : 1'bz;  // Controlled_Buffer controlled_buffer_6
  assign data_out[6] = en[6] ? data_in[6] : 1'bz;  // Controlled_Buffer controlled_buffer_7
  assign data_out[7] = en[7] ? data_in[7] : 1'bz;  // Controlled_Buffer controlled_buffer_8
endmodule

module compare (
  input  [7:0] a,
  input  [7:0] b,
  input  en,
  output eq
);

  wire comparator_1_eq;

  Comparator #(.mode("unsigned")) comparator_1 (.a(a), .b(b), .eq(comparator_1_eq));  // open: gt, lt
  assign eq = en ? comparator_1_eq : 1'bz;  // Controlled_Buffer controlled_buffer_1
endmodule

module prescaler (
  input  en,
  input  clk,
  input  rst,
  input  [7:0] freq_sel,
  output clk_out
);

  wire and_1_out, t_ff_1_q, t_ff_2_q, t_ff_3_q;

  and and_1 (and_1_out, en, clk);
  T_Flip_Flop t_ff_1 (.T(1'b1), .clk(and_1_out), .Q(t_ff_1_q), .reset(rst));  // open: Qn, preset
  T_Flip_Flop t_ff_2 (.T(1'b1), .clk(t_ff_1_q), .Q(t_ff_2_q), .reset(rst));  // open: Qn, preset
  T_Flip_Flop t_ff_3 (.T(1'b1), .clk(t_ff_2_q), .Q(t_ff_3_q), .reset(rst));  // open: Qn, preset
  Multiplexer #(.select(2)) multiplexer_1 (
    .in0(and_1_out), .in1(t_ff_1_q), .in2(t_ff_2_q), .in3(t_ff_3_q), .out(clk_out), .sel(freq_sel[3:2]));
endmodule
