// Logisim project rsicv_cpus.circ as structural Verilog: 22 circuits, main circuit cpu_single_cycle
module cpu_single_cycle (
  input  [31:0] data_in,
  input  rst,
  input  clk,
  input  hld,
  output [31:0] addr,
  output mem_rd,
  output mem_wr,
  output [31:0] data_out,
  output [1:0] data_type,
  output hlda
);

  wire and_1_out, and_2_out, branch_1_tk, control_decode_1_addr_src, control_decode_1_alu_a,
       control_decode_1_alu_b, control_decode_1_br, control_decode_1_jp, control_decode_1_rf_we,
       hold_unit_1_cclk, not_1_out, or_1_out;
  wire [1:0] control_decode_1_alu_op, control_decode_1_rf_src;
  wire [2:2] control_decode_1_func3;
  wire [4:0] control_decode_1_rd, control_decode_1_rs1, control_decode_1_rs2;
  wire [6:0] control_decode_1_func7;
  wire [31:0] addr_bit0_clr_1_res, alu_1_res, control_decode_1_instr, data_alignment_1_data_out,
       imm_gen_1_imm, multiplexer_1_out, multiplexer_2_out, multiplexer_3_out, multiplexer_4_out,
       multiplexer_5_out, plus_4_1_res, register_1_q, register_file_1_a_out;

  Multiplexer #(.width(32)) multiplexer_1 (
    .in0(plus_4_1_res), .in1(addr_bit0_clr_1_res), .out(multiplexer_1_out), .sel(or_1_out));
  addr_bit0_clr addr_bit0_clr_1 (.res(addr_bit0_clr_1_res), .data(alu_1_res));
  assign addr = not_1_out ? multiplexer_2_out : 32'bz;  // Controlled_Buffer controlled_buffer_1
  Multiplexer #(.width(32)) multiplexer_2 (
    .in0(register_1_q), .in1(alu_1_res), .out(multiplexer_2_out), .sel(control_decode_1_addr_src));
  Register #(.trigger("falling"), .width(32)) register_1 (
    .D(multiplexer_1_out), .en(and_1_out), .Q(register_1_q), .clk(hold_unit_1_cclk), .clr(rst));
  and and_1 (and_1_out, ~control_decode_1_addr_src, not_1_out);  // AND_Gate
  not not_1 (not_1_out, hlda);
  plus_4 plus_4_1 (.res(plus_4_1_res), .data(register_1_q));
  control_decode control_decode_1 (
    .addr_src(control_decode_1_addr_src), .jp(control_decode_1_jp), .br(control_decode_1_br),
    .rf_src(control_decode_1_rf_src), .rf_we(control_decode_1_rf_we), .alu_op(control_decode_1_alu_op),
    .alu_a(control_decode_1_alu_a), .alu_b(control_decode_1_alu_b), .mem_rd(mem_rd), .mem_wr(mem_wr),
    .rd(control_decode_1_rd), .func3({control_decode_1_func3[2], data_type}), .rs1(control_decode_1_rs1),
    .rs2(control_decode_1_rs2), .func7(control_decode_1_func7), .instr(control_decode_1_instr),
    .clk(hold_unit_1_cclk), .rst(rst), .instr_in(data_in));
  register_file register_file_1 (
    .b_out(data_out), .a_out(register_file_1_a_out), .we(control_decode_1_rf_we), .rs2(control_decode_1_rs2),
    .rst(rst), .clk(hold_unit_1_cclk), .rs1(control_decode_1_rs1), .rd(control_decode_1_rd),
    .data(multiplexer_5_out));
  imm_gen imm_gen_1 (.imm(imm_gen_1_imm), .instr(control_decode_1_instr));
  Multiplexer #(.width(32)) multiplexer_3 (
    .in0(register_file_1_a_out), .in1(register_1_q), .out(multiplexer_3_out), .sel(control_decode_1_alu_a));
  Multiplexer #(.width(32)) multiplexer_4 (
    .in0(data_out), .in1(imm_gen_1_imm), .out(multiplexer_4_out), .sel(control_decode_1_alu_b));
  branch branch_1 (
    .tk(branch_1_tk), .func3({control_decode_1_func3[2], data_type}), .a(register_file_1_a_out), .b(data_out));
  or or_1 (or_1_out, control_decode_1_jp, and_2_out);
  and and_2 (and_2_out, control_decode_1_br, branch_1_tk);
  alu alu_1 (
    .res(alu_1_res), .alu_op(control_decode_1_alu_op), .func3({control_decode_1_func3[2], data_type}),
    .a(multiplexer_3_out), .b(multiplexer_4_out), .func7(control_decode_1_func7));
  data_alignment data_alignment_1 (
    .data_out(data_alignment_1_data_out), .data_type({control_decode_1_func3[2], data_type}),
    .data_in(data_in));
  Multiplexer #(.select(2), .width(32)) multiplexer_5 (
    .in0(data_alignment_1_data_out), .in1(plus_4_1_res), .in2(alu_1_res), .out(multiplexer_5_out),
    .sel(control_decode_1_rf_src));  // open: in3
  hold_unit hold_unit_1 (
    .hlda(hlda), .cclk(hold_unit_1_cclk), .hld(hld), .ma(control_decode_1_addr_src), .rst(rst), .clk(clk));
endmodule

module cpu_5_stage_pipeline (
  input  [31:0] data_in,
  input  rst,
  input  clk,
  input  hld,
  output [31:0] addr,
  output mem_rd,
  output mem_wr,
  output [31:0] data_out,
  output [1:0] data_type,
  output hlda
);

  wire and_1_out, and_2_out, branch_1_tk, forwarding_unit_1_fwa, forwarding_unit_1_fwb,
       hazard_unit_1_addr_src, hazard_unit_1_flush, hazard_unit_1_pc_en, hold_unit_1_cclk, not_1_out,
       or_1_out, pipe_de_ex_1_alu_a, pipe_de_ex_1_alu_b, pipe_de_ex_1_br, pipe_de_ex_1_jp,
       pipe_ex_ma_1_jb_ma, pipe_ex_ma_1_rf_we, pipe_mm_wb_1_rf_we;
  wire [1:0] pipe_de_ex_1_alu_op, pipe_mm_wb_1_rf_src;
  wire [2:0] pipe_de_ex_1_func3;
  wire [2:2] pipe_ex_ma_1_func3;
  wire [4:0] pipe_de_ex_1_rd, pipe_de_ex_1_rs1, pipe_de_ex_1_rs2, pipe_ex_ma_1_rd, pipe_if_de_1_rs1,
       pipe_if_de_1_rs2, pipe_mm_wb_1_rd;
  wire [6:0] pipe_de_ex_1_func7;
  wire [10:0] control_word_gen_1_ctrl_word, pipe_de_ex_1_ctrl_word, pipe_ex_ma_1_ctrl_word;
  wire [31:0] addr_bit0_clr_1_res, alu_1_res, data_alignment_1_data_out, ex_operand_1_alu_opr,
       ex_operand_1_br_opr, ex_operand_2_alu_opr, ex_operand_2_br_opr, forwarding_unit_1_a,
       forwarding_unit_1_b, imm_gen_1_imm, multiplexer_1_out, multiplexer_2_out, multiplexer_3_out,
       multiplexer_4_out, pipe_de_ex_1_imm_gen, pipe_de_ex_1_npc, pipe_de_ex_1_pc, pipe_de_ex_1_ra,
       pipe_de_ex_1_rb, pipe_ex_ma_1_alu_res, pipe_ex_ma_1_npc, pipe_if_de_1_instr, pipe_if_de_1_npc,
       pipe_if_de_1_pc, pipe_mm_wb_1_alures, pipe_mm_wb_1_mem_data, pipe_mm_wb_1_npc, plus_4_1_res,
       register_1_q, register_file_1_a_out, register_file_1_b_out;

  addr_bit0_clr addr_bit0_clr_1 (.res(addr_bit0_clr_1_res), .data(alu_1_res));
  assign addr = not_1_out ? multiplexer_1_out : 32'bz;  // Controlled_Buffer controlled_buffer_1
  Multiplexer #(.width(32)) multiplexer_1 (
    .in0(register_1_q), .in1(pipe_ex_ma_1_alu_res), .out(multiplexer_1_out), .sel(hazard_unit_1_addr_src));
  Multiplexer #(.width(32)) multiplexer_2 (
    .in0(plus_4_1_res), .in1(addr_bit0_clr_1_res), .out(multiplexer_2_out), .sel(or_1_out));
  and and_1 (and_1_out, not_1_out, hazard_unit_1_pc_en);
  not not_1 (not_1_out, hlda);
  Register #(.width(32)) register_1 (
    .D(multiplexer_2_out), .en(and_1_out), .Q(register_1_q), .clk(hold_unit_1_cclk), .clr(rst));
  plus_4 plus_4_1 (.res(plus_4_1_res), .data(register_1_q));
  pipe_if_de pipe_if_de_1 (
    .instr(pipe_if_de_1_instr), .rs1(pipe_if_de_1_rs1), .rs2(pipe_if_de_1_rs2), .pc(pipe_if_de_1_pc),
    .npc(pipe_if_de_1_npc), .pc_en(hazard_unit_1_pc_en), .clk(hold_unit_1_cclk), .clr(hazard_unit_1_flush),
    .instr_i(data_in), .pc_i(register_1_q), .npc_i(plus_4_1_res));
  register_file register_file_1 (
    .b_out(register_file_1_b_out), .a_out(register_file_1_a_out), .we(pipe_mm_wb_1_rf_we),
    .rs2(pipe_if_de_1_rs2), .rst(rst), .clk(hold_unit_1_cclk), .rs1(pipe_if_de_1_rs1), .rd(pipe_mm_wb_1_rd),
    .data(multiplexer_4_out));
  imm_gen imm_gen_1 (.imm(imm_gen_1_imm), .instr(pipe_if_de_1_instr));
  control_word_gen control_word_gen_1 (.ctrl_word(control_word_gen_1_ctrl_word), .instr(pipe_if_de_1_instr));
  pipe_de_ex pipe_de_ex_1 (
    .rb(pipe_de_ex_1_rb), .rd(pipe_de_ex_1_rd), .func3(pipe_de_ex_1_func3), .rs1(pipe_de_ex_1_rs1),
    .rs2(pipe_de_ex_1_rs2), .func7(pipe_de_ex_1_func7), .pc(pipe_de_ex_1_pc), .npc(pipe_de_ex_1_npc),
    .ra(pipe_de_ex_1_ra), .imm_gen(pipe_de_ex_1_imm_gen), .ctrl_word(pipe_de_ex_1_ctrl_word),
    .jp(pipe_de_ex_1_jp), .br(pipe_de_ex_1_br), .alu_op(pipe_de_ex_1_alu_op), .alu_a(pipe_de_ex_1_alu_a),
    .alu_b(pipe_de_ex_1_alu_b), .clk(hold_unit_1_cclk), .clr(hazard_unit_1_flush),
    .ctrl_word_in(control_word_gen_1_ctrl_word), .rb_in(register_file_1_b_out), .instr(pipe_if_de_1_instr),
    .pc_in(pipe_if_de_1_pc), .npc_in(pipe_if_de_1_npc), .ra_i(register_file_1_a_out),
    .imm_gen_in(imm_gen_1_imm));
  forwarding_unit forwarding_unit_1 (
    .b(forwarding_unit_1_b), .fwA(forwarding_unit_1_fwa), .fwB(forwarding_unit_1_fwb),
    .a(forwarding_unit_1_a), .wb_rf_we(pipe_mm_wb_1_rf_we), .ma_rf_we(pipe_ex_ma_1_rf_we),
    .rs1(pipe_de_ex_1_rs1), .wb_rd(pipe_mm_wb_1_rd), .ma_rd(pipe_ex_ma_1_rd), .rs2(pipe_de_ex_1_rs2),
    .wb_data(multiplexer_4_out), .ma_data(multiplexer_3_out));
  hazard_unit hazard_unit_1 (
    .addr_src(hazard_unit_1_addr_src), .pc_en(hazard_unit_1_pc_en), .flush(hazard_unit_1_flush), .wr(mem_wr),
    .rst(rst), .jb_ex(or_1_out), .clk(hold_unit_1_cclk), .jb_ma(pipe_ex_ma_1_jb_ma), .rd(mem_rd));
  ex_operand ex_operand_1 (
    .br_opr(ex_operand_1_br_opr), .alu_opr(ex_operand_1_alu_opr), .op2(pipe_de_ex_1_pc),
    .fw(forwarding_unit_1_fwa), .rsel(pipe_de_ex_1_alu_a), .op1(pipe_de_ex_1_ra), .fw_op(forwarding_unit_1_a));
  ex_operand ex_operand_2 (
    .br_opr(ex_operand_2_br_opr), .alu_opr(ex_operand_2_alu_opr), .op2(pipe_de_ex_1_imm_gen),
    .fw(forwarding_unit_1_fwb), .rsel(pipe_de_ex_1_alu_b), .op1(pipe_de_ex_1_rb), .fw_op(forwarding_unit_1_b));
  and and_2 (and_2_out, pipe_de_ex_1_br, branch_1_tk);
  branch branch_1 (.tk(branch_1_tk), .func3(pipe_de_ex_1_func3), .a(ex_operand_1_br_opr), .b(ex_operand_2_br_opr));
  alu alu_1 (
    .res(alu_1_res), .alu_op(pipe_de_ex_1_alu_op), .func3(pipe_de_ex_1_func3), .a(ex_operand_1_alu_opr),
    .b(ex_operand_2_alu_opr), .func7(pipe_de_ex_1_func7));
  pipe_ex_ma pipe_ex_ma_1 (
    .jb_ma(pipe_ex_ma_1_jb_ma), .alu_res(pipe_ex_ma_1_alu_res), .func3({pipe_ex_ma_1_func3[2], data_type}),
    .rb(data_out), .npc(pipe_ex_ma_1_npc), .rd(pipe_ex_ma_1_rd), .ctrl_word(pipe_ex_ma_1_ctrl_word),
    .mem_rd(mem_rd), .mem_wr(mem_wr), .rf_we(pipe_ex_ma_1_rf_we), .ctrl_word_in(pipe_de_ex_1_ctrl_word),
    .clk(hold_unit_1_cclk), .clr(rst), .jb(or_1_out), .rd_in(pipe_de_ex_1_rd), .func3_in(pipe_de_ex_1_func3),
    .aluRes_in(alu_1_res), .rb_in(ex_operand_2_br_opr), .npc_in(pipe_de_ex_1_npc));
  or or_1 (or_1_out, pipe_de_ex_1_jp, and_2_out);
  data_alignment data_alignment_1 (
    .data_out(data_alignment_1_data_out), .data_type({pipe_ex_ma_1_func3[2], data_type}), .data_in(data_in));
  Multiplexer #(.width(32)) multiplexer_3 (
    .in0(pipe_ex_ma_1_alu_res), .in1(data_alignment_1_data_out), .out(multiplexer_3_out), .sel(mem_rd));
  pipe_mm_wb pipe_mm_wb_1 (
    .mem_data(pipe_mm_wb_1_mem_data), .aluRes(pipe_mm_wb_1_alures), .npc(pipe_mm_wb_1_npc),
    .rd(pipe_mm_wb_1_rd), .rf_src(pipe_mm_wb_1_rf_src), .rf_we(pipe_mm_wb_1_rf_we), .clk(hold_unit_1_cclk),
    .clr(rst), .rd_in(pipe_ex_ma_1_rd), .ctrl_word_in(pipe_ex_ma_1_ctrl_word),
    .mem_data_in(data_alignment_1_data_out), .aluRes_in(pipe_ex_ma_1_alu_res), .npc_in(pipe_ex_ma_1_npc));
  Multiplexer #(.select(2), .width(32)) multiplexer_4 (
    .in0(pipe_mm_wb_1_mem_data), .in1(pipe_mm_wb_1_npc), .in2(pipe_mm_wb_1_alures), .out(multiplexer_4_out),
    .sel(pipe_mm_wb_1_rf_src));  // open: in3
  hold_unit hold_unit_1 (
    .hlda(hlda), .cclk(hold_unit_1_cclk), .hld(hld), .ma(hazard_unit_1_addr_src), .rst(rst), .clk(clk));

  // Notes on the sheet:
  //   A
  //   B
endmodule

module alu (
  input  [31:0] a,
  input  [31:0] b,
  input  [1:0] alu_op,
  input  [6:0] func7,
  input  [2:0] func3,
  output [31:0] res
);

  wire alu_ctrl_1_a_en, alu_ctrl_1_func3_en, alu_ctrl_1_func_mux, comparator_1_lt, comparator_2_lt;
  wire [3:0] controlled_buffer_2_out;
  wire [31:0] adder_1_out, and_1_out, bit_extender_1_out, bit_extender_2_out, controlled_buffer_1_out,
       divider_1_out, divider_1_rem, divider_2_out, divider_2_rem, multiplexer_1_out, multiplexer_2_out,
       multiplier_1_out, or_1_out, shifter_1_out, shifter_2_out, shifter_3_out, subtractor_1_out, xor_1_out;
  wire [32:0] bit_extender_3_out, bit_extender_4_out, bit_extender_5_out, bit_extender_6_out,
       bit_extender_7_out, bit_extender_8_out, multiplier_2_out, multiplier_3_out, multiplier_4_out;

  alu_ctrl alu_ctrl_1 (
    .a_en(alu_ctrl_1_a_en), .func_mux(alu_ctrl_1_func_mux), .m_ext(controlled_buffer_2_out[3]),
    .func3_en(alu_ctrl_1_func3_en), .alu_op(alu_op), .func7(func7));
  assign controlled_buffer_1_out = alu_ctrl_1_a_en ? a : 32'bz;  // Controlled_Buffer controlled_buffer_1
  assign controlled_buffer_2_out[2:0] = alu_ctrl_1_func3_en ? func3 : 3'bz;  // Controlled_Buffer controlled_buffer_2
  Pull_Resistor pull_resistor_1 (.node(controlled_buffer_2_out[2:0]));
  Pull_Resistor pull_resistor_2 (.node(controlled_buffer_1_out));
  Adder #(.width(32)) adder_1 (.a(controlled_buffer_1_out), .b(b), .out(adder_1_out));  // open: cin, cout
  Subtractor #(.width(32)) subtractor_1 (
    .a(controlled_buffer_1_out), .b(b), .out(subtractor_1_out));  // open: bin, bout
  Shifter #(.width(32)) shifter_1 (.in(controlled_buffer_1_out), .\dist (b[4:0]), .out(shifter_1_out));
  Comparator #(.width(32)) comparator_1 (.a(controlled_buffer_1_out), .b(b), .lt(comparator_1_lt));  // open: gt, eq
  assign bit_extender_1_out = {{31{1'b0}}, comparator_1_lt};  // Bit_Extender bit_extender_1
  Comparator #(.mode("unsigned"), .width(32)) comparator_2 (
    .a(controlled_buffer_1_out), .b(b), .lt(comparator_2_lt));  // open: gt, eq
  assign bit_extender_2_out = {{31{1'b0}}, comparator_2_lt};  // Bit_Extender bit_extender_2
  assign xor_1_out = controlled_buffer_1_out ^ b;  // XOR_Gate xor_1, 32 bits wide
  Shifter #(.shift("lr"), .width(32)) shifter_2 (.in(controlled_buffer_1_out), .\dist (b[4:0]), .out(shifter_2_out));
  Multiplexer #(.width(32)) multiplexer_1 (
    .in0(shifter_2_out), .in1(shifter_3_out), .out(multiplexer_1_out), .sel(alu_ctrl_1_func_mux));
  Shifter #(.shift("ar"), .width(32)) shifter_3 (.in(controlled_buffer_1_out), .\dist (b[4:0]), .out(shifter_3_out));
  assign or_1_out = controlled_buffer_1_out | b;  // OR_Gate or_1, 32 bits wide
  assign and_1_out = controlled_buffer_1_out & b;  // AND_Gate and_1, 32 bits wide
  Multiplier #(.width(32)) multiplier_1 (
    .a(controlled_buffer_1_out), .b(b), .out(multiplier_1_out));  // open: cin, cout
  assign bit_extender_3_out = {{1{controlled_buffer_1_out[31]}}, controlled_buffer_1_out};  // Bit_Extender bit_extender_3
  assign bit_extender_4_out = {{1{b[31]}}, b};  // Bit_Extender bit_extender_4
  assign bit_extender_5_out = {{1{1'b0}}, controlled_buffer_1_out};  // Bit_Extender bit_extender_5
  assign bit_extender_6_out = {{1{1'b0}}, b};  // Bit_Extender bit_extender_6
  assign bit_extender_7_out = {{1{controlled_buffer_1_out[31]}}, controlled_buffer_1_out};  // Bit_Extender bit_extender_7
  assign bit_extender_8_out = {{1{1'b0}}, b};  // Bit_Extender bit_extender_8
  Divider #(.mode("twosComplement"), .width(32)) divider_1 (
    .a(controlled_buffer_1_out), .b(b), .out(divider_1_out), .rem(divider_1_rem));  // open: upper
  Divider #(.width(32)) divider_2 (
    .a(controlled_buffer_1_out), .b(b), .out(divider_2_out), .rem(divider_2_rem));  // open: upper
  Multiplexer #(.width(32)) multiplexer_2 (
    .in0(adder_1_out), .in1(subtractor_1_out), .out(multiplexer_2_out), .sel(alu_ctrl_1_func_mux));
  Multiplier #(.width(33)) multiplier_2 (
    .a(bit_extender_3_out), .b(bit_extender_4_out), .out(multiplier_2_out));  // open: cin, cout
  Multiplier #(.width(33)) multiplier_3 (
    .a(bit_extender_5_out), .b(bit_extender_6_out), .out(multiplier_3_out));  // open: cin, cout
  Multiplier #(.width(33)) multiplier_4 (
    .a(bit_extender_7_out), .b(bit_extender_8_out), .out(multiplier_4_out));  // open: cin, cout
  Multiplexer #(.select(4), .width(32)) multiplexer_3 (
    .in0(multiplexer_2_out), .in1(shifter_1_out), .in2(bit_extender_1_out), .in3(bit_extender_2_out),
    .in4(xor_1_out), .in5(multiplexer_1_out), .in6(or_1_out), .in7(and_1_out), .in8(multiplier_1_out),
    .in9(multiplier_2_out[31:0]), .in10(multiplier_3_out[31:0]), .in11(multiplier_4_out[31:0]),
    .in12(divider_1_out), .in13(divider_2_out), .in14(divider_1_rem), .in15(divider_2_rem), .out(res),
    .sel(controlled_buffer_2_out));
endmodule

module alu_ctrl (
  input  [1:0] alu_op,
  input  [6:0] func7,
  output a_en,
  output func_mux,
  output m_ext,
  output func3_en
);

  wire [2:0] comparator_1_eq;

  Comparator #(.mode("unsigned"), .width(7)) comparator_1 (
    .a(func7), .b({7{1'b0}}), .eq(comparator_1_eq[0]));  // open: gt, lt
  Comparator #(.mode("unsigned"), .width(7)) comparator_2 (
    .a(func7), .b(7'b0100000), .eq(comparator_1_eq[1]));  // open: gt, lt
  Comparator #(.mode("unsigned"), .width(7)) comparator_3 (
    .a(func7), .b(7'b0000001), .eq(comparator_1_eq[2]));  // open: gt, lt
  PLA #(.in_width(5), .out_width(4), .\table ("xxx00 0001 # ADD\n00101 1001 # RR0\n01001 1011 # RR1\n10001 1101 # RRM\nxxx11 1001 # RI\nxxx10 0000 # LUI")) pla_1 (
    .in({comparator_1_eq, alu_op}), .out({func3_en, m_ext, func_mux, a_en}));
endmodule

module ex_operand (
  input  [31:0] op1,
  input  [31:0] fw_op,
  input  [31:0] op2,
  input  fw,
  input  rsel,
  output [31:0] br_opr,
  output [31:0] alu_opr
);

  Multiplexer #(.width(32)) multiplexer_1 (.in0(op1), .in1(fw_op), .out(br_opr), .sel(fw));
  Multiplexer #(.width(32)) multiplexer_2 (.in0(br_opr), .in1(op2), .out(alu_opr), .sel(rsel));
endmodule

module register_file (
  input  [4:0] rs1,
  input  [4:0] rs2,
  input  rst,
  input  [31:0] data,
  input  clk,
  input  [4:0] rd,
  input  we,
  output [31:0] a_out,
  output [31:0] b_out
);

  wire [31:0] decoder_1_out0, register_1_q, register_2_q, register_3_q, register_4_q, register_5_q,
       register_6_q, register_7_q, register_8_q, register_9_q, register_10_q, register_11_q, register_12_q,
       register_13_q, register_14_q, register_15_q, register_16_q, register_17_q, register_18_q,
       register_19_q, register_20_q, register_21_q, register_22_q, register_23_q, register_24_q,
       register_25_q, register_26_q, register_27_q, register_28_q, register_29_q, register_30_q,
       register_31_q;

  Multiplexer #(.select(5), .width(32)) multiplexer_1 (
    .in0({32{1'b0}}), .in1(register_29_q), .in2(register_27_q), .in3(register_25_q), .in4(register_24_q),
    .in5(register_21_q), .in6(register_19_q), .in7(register_16_q), .in8(register_17_q), .in9(register_13_q),
    .in10(register_11_q), .in11(register_9_q), .in12(register_8_q), .in13(register_5_q), .in14(register_3_q),
    .in15(register_1_q), .in16(register_31_q), .in17(register_30_q), .in18(register_28_q),
    .in19(register_26_q), .in20(register_23_q), .in21(register_22_q), .in22(register_20_q),
    .in23(register_18_q), .in24(register_15_q), .in25(register_14_q), .in26(register_12_q),
    .in27(register_10_q), .in28(register_7_q), .in29(register_6_q), .in30(register_4_q), .in31(register_2_q),
    .out(a_out), .sel(rs1));
  Decoder #(.select(5)) decoder_1 (
    .out0(decoder_1_out0[0]), .out1(decoder_1_out0[1]), .out2(decoder_1_out0[2]), .out3(decoder_1_out0[3]),
    .out4(decoder_1_out0[4]), .out5(decoder_1_out0[5]), .out6(decoder_1_out0[6]), .out7(decoder_1_out0[7]),
    .out8(decoder_1_out0[8]), .out9(decoder_1_out0[9]), .out10(decoder_1_out0[10]),
    .out11(decoder_1_out0[11]), .out12(decoder_1_out0[12]), .out13(decoder_1_out0[13]),
    .out14(decoder_1_out0[14]), .out15(decoder_1_out0[15]), .out16(decoder_1_out0[16]),
    .out17(decoder_1_out0[17]), .out18(decoder_1_out0[18]), .out19(decoder_1_out0[19]),
    .out20(decoder_1_out0[20]), .out21(decoder_1_out0[21]), .out22(decoder_1_out0[22]),
    .out23(decoder_1_out0[23]), .out24(decoder_1_out0[24]), .out25(decoder_1_out0[25]),
    .out26(decoder_1_out0[26]), .out27(decoder_1_out0[27]), .out28(decoder_1_out0[28]),
    .out29(decoder_1_out0[29]), .out30(decoder_1_out0[30]), .out31(decoder_1_out0[31]), .sel(rd), .en(we));
  Register #(.trigger("falling"), .width(32)) register_1 (
    .D(data), .en(decoder_1_out0[15]), .Q(register_1_q), .clk(clk), .clr(rst));
  Register #(.trigger("falling"), .width(32)) register_2 (
    .D(data), .en(decoder_1_out0[31]), .Q(register_2_q), .clk(clk), .clr(rst));
  Register #(.trigger("falling"), .width(32)) register_3 (
    .D(data), .en(decoder_1_out0[14]), .Q(register_3_q), .clk(clk), .clr(rst));
  Register #(.trigger("falling"), .width(32)) register_4 (
    .D(data), .en(decoder_1_out0[30]), .Q(register_4_q), .clk(clk), .clr(rst));
  Register #(.trigger("falling"), .width(32)) register_5 (
    .D(data), .en(decoder_1_out0[13]), .Q(register_5_q), .clk(clk), .clr(rst));
  Register #(.trigger("falling"), .width(32)) register_6 (
    .D(data), .en(decoder_1_out0[29]), .Q(register_6_q), .clk(clk), .clr(rst));
  Register #(.trigger("falling"), .width(32)) register_7 (
    .D(data), .en(decoder_1_out0[28]), .Q(register_7_q), .clk(clk), .clr(rst));
  Register #(.trigger("falling"), .width(32)) register_8 (
    .D(data), .en(decoder_1_out0[12]), .Q(register_8_q), .clk(clk), .clr(rst));
  Register #(.trigger("falling"), .width(32)) register_9 (
    .D(data), .en(decoder_1_out0[11]), .Q(register_9_q), .clk(clk), .clr(rst));
  Register #(.trigger("falling"), .width(32)) register_10 (
    .D(data), .en(decoder_1_out0[27]), .Q(register_10_q), .clk(clk), .clr(rst));
  Register #(.trigger("falling"), .width(32)) register_11 (
    .D(data), .en(decoder_1_out0[10]), .Q(register_11_q), .clk(clk), .clr(rst));
  Register #(.trigger("falling"), .width(32)) register_12 (
    .D(data), .en(decoder_1_out0[26]), .Q(register_12_q), .clk(clk), .clr(rst));
  Register #(.trigger("falling"), .width(32)) register_13 (
    .D(data), .en(decoder_1_out0[9]), .Q(register_13_q), .clk(clk), .clr(rst));
  Register #(.trigger("falling"), .width(32)) register_14 (
    .D(data), .en(decoder_1_out0[25]), .Q(register_14_q), .clk(clk), .clr(rst));
  Register #(.trigger("falling"), .width(32)) register_15 (
    .D(data), .en(decoder_1_out0[24]), .Q(register_15_q), .clk(clk), .clr(rst));
  Register #(.trigger("falling"), .width(32)) register_16 (
    .D(data), .en(decoder_1_out0[7]), .Q(register_16_q), .clk(clk), .clr(rst));
  Register #(.trigger("falling"), .width(32)) register_17 (
    .D(data), .en(decoder_1_out0[8]), .Q(register_17_q), .clk(clk), .clr(rst));
  Register #(.trigger("falling"), .width(32)) register_18 (
    .D(data), .en(decoder_1_out0[23]), .Q(register_18_q), .clk(clk), .clr(rst));
  Register #(.trigger("falling"), .width(32)) register_19 (
    .D(data), .en(decoder_1_out0[6]), .Q(register_19_q), .clk(clk), .clr(rst));
  Register #(.trigger("falling"), .width(32)) register_20 (
    .D(data), .en(decoder_1_out0[22]), .Q(register_20_q), .clk(clk), .clr(rst));
  Register #(.trigger("falling"), .width(32)) register_21 (
    .D(data), .en(decoder_1_out0[5]), .Q(register_21_q), .clk(clk), .clr(rst));
  Register #(.trigger("falling"), .width(32)) register_22 (
    .D(data), .en(decoder_1_out0[21]), .Q(register_22_q), .clk(clk), .clr(rst));
  Register #(.trigger("falling"), .width(32)) register_23 (
    .D(data), .en(decoder_1_out0[20]), .Q(register_23_q), .clk(clk), .clr(rst));
  Register #(.trigger("falling"), .width(32)) register_24 (
    .D(data), .en(decoder_1_out0[4]), .Q(register_24_q), .clk(clk), .clr(rst));
  Register #(.trigger("falling"), .width(32)) register_25 (
    .D(data), .en(decoder_1_out0[3]), .Q(register_25_q), .clk(clk), .clr(rst));
  Register #(.trigger("falling"), .width(32)) register_26 (
    .D(data), .en(decoder_1_out0[19]), .Q(register_26_q), .clk(clk), .clr(rst));
  Register #(.trigger("falling"), .width(32)) register_27 (
    .D(data), .en(decoder_1_out0[2]), .Q(register_27_q), .clk(clk), .clr(rst));
  Register #(.trigger("falling"), .width(32)) register_28 (
    .D(data), .en(decoder_1_out0[18]), .Q(register_28_q), .clk(clk), .clr(rst));
  Register #(.trigger("falling"), .width(32)) register_29 (
    .D(data), .en(decoder_1_out0[1]), .Q(register_29_q), .clk(clk), .clr(rst));
  Register #(.trigger("falling"), .width(32)) register_30 (
    .D(data), .en(decoder_1_out0[17]), .Q(register_30_q), .clk(clk), .clr(rst));
  Register #(.trigger("falling"), .width(32)) register_31 (
    .D(data), .en(decoder_1_out0[16]), .Q(register_31_q), .clk(clk), .clr(rst));
  Multiplexer #(.select(5), .width(32)) multiplexer_2 (
    .in0({32{1'b0}}), .in1(register_29_q), .in2(register_27_q), .in3(register_25_q), .in4(register_24_q),
    .in5(register_21_q), .in6(register_19_q), .in7(register_16_q), .in8(register_17_q), .in9(register_13_q),
    .in10(register_11_q), .in11(register_9_q), .in12(register_8_q), .in13(register_5_q), .in14(register_3_q),
    .in15(register_1_q), .in16(register_31_q), .in17(register_30_q), .in18(register_28_q),
    .in19(register_26_q), .in20(register_23_q), .in21(register_22_q), .in22(register_20_q),
    .in23(register_18_q), .in24(register_15_q), .in25(register_14_q), .in26(register_12_q),
    .in27(register_10_q), .in28(register_7_q), .in29(register_6_q), .in30(register_4_q), .in31(register_2_q),
    .out(b_out), .sel(rs2));
endmodule

module branch (
  input  [31:0] a,
  input  [31:0] b,
  input  [2:0] func3,
  output tk
);

  wire comparator_1_eq, comparator_1_gt, comparator_1_lt, comparator_2_eq, comparator_2_gt, comparator_2_lt,
       not_1_out, or_1_out, or_2_out;

  Comparator #(.width(32)) comparator_1 (
    .a(a), .b(b), .gt(comparator_1_gt), .eq(comparator_1_eq), .lt(comparator_1_lt));
  Comparator #(.mode("unsigned"), .width(32)) comparator_2 (
    .a(a), .b(b), .gt(comparator_2_gt), .eq(comparator_2_eq), .lt(comparator_2_lt));
  or or_1 (or_1_out, comparator_2_eq, comparator_2_gt);
  not not_1 (not_1_out, comparator_1_eq);
  or or_2 (or_2_out, comparator_1_eq, comparator_1_gt);
  Multiplexer #(.select(3)) multiplexer_1 (
    .in0(comparator_1_eq), .in1(not_1_out), .in2(1'b0), .in3(1'b0), .in4(comparator_1_lt), .in5(or_2_out),
    .in6(comparator_2_lt), .in7(or_1_out), .out(tk), .sel(func3));
endmodule

module control_decode (
  input  [31:0] instr_in,
  input  clk,
  input  rst,
  output jp,
  output br,
  output [1:0] rf_src,
  output rf_we,
  output [1:0] alu_op,
  output alu_a,
  output alu_b,
  output mem_rd,
  output addr_src,
  output mem_wr,
  output [4:0] rd,
  output [2:0] func3,
  output [4:0] rs1,
  output [4:0] rs2,
  output [6:0] func7,
  output [31:0] instr
);

  wire [31:0] nop_pull_1_instr_out;

  nop_pull nop_pull_1 (.instr_out(nop_pull_1_instr_out), .instr_in(instr_in), .nop(addr_src));
  Register #(.width(32)) register_1 (
    .D(nop_pull_1_instr_out), .Q({func7, instr[24:15], func3, instr[11:0]}), .clk(clk), .clr(rst));  // open: en
  PLA #(.in_width(7), .out_width(11), .\table ("0110111 00101011000 # LUI\n0010111 00110011000 # AUIPC\n1101111 00110010101 # JAL\n1100111 00100010101 # JALR\n1100011 00110000010 # BXX\n0000011 01100010000 # LX\n0100011 10100000000 # SX\n0010011 00101111000 # RI\n0110011 00000111000 # RR")) pla_1 (
    .in(instr[6:0]), .out({mem_wr, mem_rd, alu_b, alu_a, alu_op, rf_we, rf_src, br, jp}));
  or or_1 (addr_src, mem_rd, mem_wr);

  assign {instr[31:25], instr[14:12]} = {func7, func3};
  assign rd = instr[11:7];
  assign rs1 = instr[19:15];
  assign rs2 = instr[24:20];
endmodule

module imm_gen (
  input  [31:0] instr,
  output [31:0] imm
);

  wire [0:0] undriven, undriven_2;
  wire [2:0] pla_1_out;
  wire [11:0] bit_extender_4_out;
  wire [19:0] bit_extender_1_out;
  wire [20:0] bit_extender_2_out, bit_extender_3_out;

  assign bit_extender_1_out = {{19{instr[31]}}, instr[31]};  // Bit_Extender bit_extender_1
  assign bit_extender_2_out = {{20{instr[31]}}, instr[31]};  // Bit_Extender bit_extender_2
  assign bit_extender_3_out = {{20{instr[31]}}, instr[31]};  // Bit_Extender bit_extender_3
  assign bit_extender_4_out = {{11{instr[31]}}, instr[31]};  // Bit_Extender bit_extender_4
  Pull_Resistor pull_resistor_1 (.node(imm));
  Multiplexer #(.select(3), .width(32)) multiplexer_1 (
    .in0({instr[31:12], {12{1'b0}}}),
    .in1({bit_extender_1_out, instr[7], instr[30:25], instr[11:8], undriven[0]}),
    .in2({bit_extender_2_out, instr[30:25], instr[11:7]}), .in3({bit_extender_3_out, instr[30:20]}),
    .in4({bit_extender_4_out, instr[19:12], instr[20], instr[30:21], undriven_2[0]}), .out(imm),
    .sel(pla_1_out));  // open: in5, in6, in7
  PLA #(.in_width(5), .out_width(3), .\table ("01100 000 # U\n00101 000 # U\n11011 100 # J\n11001 011 # I\n11000 001 # B\n00000 011 # I\n01000 010 # S\n00100 011 # I\n01101 000 # U")) pla_1 (
    .in(instr[6:2]), .out(pla_1_out));

  // Notes on the sheet:
  //   U
  //   B
  //   S
  //   I
  //   J
endmodule

module pipe_if_de (
  input  pc_en,
  input  [31:0] instr_i,
  input  [31:0] pc_i,
  input  [31:0] npc_i,
  input  clk,
  input  clr,
  output [31:0] instr,
  output [4:0] rs1,
  output [4:0] rs2,
  output [31:0] pc,
  output [31:0] npc
);

  wire not_1_out;
  wire [31:0] nop_pull_1_instr_out;

  not not_1 (not_1_out, pc_en);
  nop_pull nop_pull_1 (.instr_out(nop_pull_1_instr_out), .instr_in(instr_i), .nop(not_1_out));
  Register #(.width(32)) register_1 (.D(nop_pull_1_instr_out), .Q(instr), .clk(clk), .clr(clr));  // open: en
  Register #(.width(32)) register_2 (.D(pc_i), .Q(pc), .clk(clk), .clr(clr));  // open: en
  Register #(.width(32)) register_3 (.D(npc_i), .Q(npc), .clk(clk), .clr(clr));  // open: en

  assign rs1 = instr[19:15];
  assign rs2 = instr[24:20];
endmodule

module pipe_de_ex (
  input  [31:0] ra_i,
  input  [31:0] rb_in,
  input  [31:0] instr,
  input  [31:0] pc_in,
  input  [31:0] npc_in,
  input  [31:0] imm_gen_in,
  input  [10:0] ctrl_word_in,
  input  clk,
  input  clr,
  output [31:0] ra,
  output [31:0] rb,
  output [4:0] rd,
  output [2:0] func3,
  output [4:0] rs1,
  output [4:0] rs2,
  output [6:0] func7,
  output [31:0] pc,
  output [31:0] npc,
  output [31:0] imm_gen,
  output [10:0] ctrl_word,
  output jp,
  output br,
  output [1:0] alu_op,
  output alu_a,
  output alu_b
);

  wire [6:0] register_3_q;

  Register #(.width(32)) register_1 (.D(ra_i), .Q(ra), .clk(clk), .clr(clr));  // open: en
  Register #(.width(32)) register_2 (.D(rb_in), .Q(rb), .clk(clk), .clr(clr));  // open: en
  Register #(.width(32)) register_3 (
    .D(instr), .Q({func7, rs2, rs1, func3, rd, register_3_q}), .clk(clk), .clr(clr));  // open: en
  Register #(.width(32)) register_4 (.D(pc_in), .Q(pc), .clk(clk), .clr(clr));  // open: en
  Register #(.width(32)) register_5 (.D(npc_in), .Q(npc), .clk(clk), .clr(clr));  // open: en
  Register #(.width(32)) register_6 (.D(imm_gen_in), .Q(imm_gen), .clk(clk), .clr(clr));  // open: en
  Register #(.width(11)) register_7 (
    .D(ctrl_word_in), .Q({ctrl_word[10:9], alu_b, alu_a, alu_op, ctrl_word[4:2], br, ctrl_word[0]}),
    .clk(clk), .clr(clr));  // open: en

  assign {ctrl_word[8:5], ctrl_word[1]} = {alu_b, alu_a, alu_op, br};
  assign jp = ctrl_word[0];
endmodule

module pipe_ex_ma (
  input  jb,
  input  [31:0] aluRes_in,
  input  [2:0] func3_in,
  input  [31:0] rb_in,
  input  [31:0] npc_in,
  input  [4:0] rd_in,
  input  [10:0] ctrl_word_in,
  input  clk,
  input  clr,
  output jb_ma,
  output [31:0] alu_res,
  output [2:0] func3,
  output [31:0] rb,
  output [31:0] npc,
  output [4:0] rd,
  output [10:0] ctrl_word,
  output mem_rd,
  output mem_wr,
  output rf_we
);

  Register #(.width(1)) register_1 (.D(jb), .Q(jb_ma), .clk(clk), .clr(clr));  // open: en
  Register #(.width(32)) register_2 (.D(aluRes_in), .Q(alu_res), .clk(clk), .clr(clr));  // open: en
  Register #(.width(3)) register_3 (.D(func3_in), .Q(func3), .clk(clk), .clr(clr));  // open: en
  Register #(.width(32)) register_4 (.D(rb_in), .Q(rb), .clk(clk), .clr(clr));  // open: en
  Register #(.width(32)) register_5 (.D(npc_in), .Q(npc), .clk(clk), .clr(clr));  // open: en
  Register #(.width(5)) register_6 (.D(rd_in), .Q(rd), .clk(clk), .clr(clr));  // open: en
  Register #(.width(11)) register_7 (.D(ctrl_word_in), .Q(ctrl_word), .clk(clk), .clr(clr));  // open: en

  assign mem_rd = ctrl_word[9];
  assign mem_wr = ctrl_word[10];
  assign rf_we = ctrl_word[4];
endmodule

module pipe_mm_wb (
  input  [31:0] mem_data_in,
  input  [31:0] aluRes_in,
  input  [31:0] npc_in,
  input  [4:0] rd_in,
  input  [10:0] ctrl_word_in,
  input  clk,
  input  clr,
  output [31:0] mem_data,
  output [31:0] aluRes,
  output [31:0] npc,
  output [4:0] rd,
  output [1:0] rf_src,
  output rf_we
);

  wire [10:0] register_5_q;

  Register #(.width(32)) register_1 (.D(mem_data_in), .Q(mem_data), .clk(clk), .clr(clr));  // open: en
  Register #(.width(32)) register_2 (.D(aluRes_in), .Q(aluRes), .clk(clk), .clr(clr));  // open: en
  Register #(.width(32)) register_3 (.D(npc_in), .Q(npc), .clk(clk), .clr(clr));  // open: en
  Register #(.width(5)) register_4 (.D(rd_in), .Q(rd), .clk(clk), .clr(clr));  // open: en
  Register #(.width(11)) register_5 (
    .D(ctrl_word_in), .Q({register_5_q[10:5], rf_we, rf_src, register_5_q[1:0]}), .clk(clk), .clr(clr));  // open: en
endmodule

module plus_4 (
  input  [31:0] data,
  output [31:0] res
);

  Adder #(.width(32)) adder_1 (.a(data), .b(32'h4), .out(res));  // open: cin, cout
endmodule

module control_word_gen (
  input  [31:0] instr,
  output [10:0] ctrl_word
);

  PLA #(.in_width(7), .out_width(11), .\table ("0110111 00101011000 # LUI\n0010111 00110011000 # AUIPC\n1101111 00110010101 # JAL\n1100111 00100010101 # JALR\n1100011 00110000010 # BXX\n0000011 01100010000 # LX\n0100011 10100000000 # SX\n0010011 00101111000 # RI\n0110011 00000111000 # RR")) pla_1 (
    .in(instr[6:0]), .out(ctrl_word));
endmodule

module addr_bit0_clr (
  input  [31:0] data,
  output [31:0] res
);

  assign res = data & ~32'h1;  // AND_Gate and_1, 32 bits wide
endmodule

module hazard_unit (
  input  rd,
  input  wr,
  input  rst,
  input  jb_ex,
  input  clk,
  input  jb_ma,
  output addr_src,
  output pc_en,
  output flush
);

  wire d_ff_1_q;

  D_Flip_Flop d_ff_1 (.D(jb_ex), .clk(clk), .Q(d_ff_1_q), .reset(jb_ma));  // open: Qn, preset
  or or_1 (addr_src, rd, wr);
  or or_2 (flush, rst, d_ff_1_q);
  or or_3 (pc_en, ~addr_src, jb_ex);  // OR_Gate
endmodule

module data_alignment (
  input  [31:0] data_in,
  input  [2:0] data_type,
  output [31:0] data_out
);

  wire [31:0] bit_extender_1_out, bit_extender_2_out, bit_extender_3_out, bit_extender_4_out;

  Multiplexer #(.select(3), .width(32)) multiplexer_1 (
    .in0(bit_extender_1_out), .in1(bit_extender_2_out), .in2(data_in), .in3({32{1'b0}}),
    .in4(bit_extender_3_out), .in5(bit_extender_4_out), .in6({32{1'b0}}), .in7({32{1'b0}}), .out(data_out));  // open: sel
  assign bit_extender_1_out = {{24{data_in[7]}}, data_in[7:0]};  // Bit_Extender bit_extender_1
  assign bit_extender_2_out = {{16{data_in[15]}}, data_in[15:0]};  // Bit_Extender bit_extender_2
  assign bit_extender_3_out = {{24{1'b0}}, data_in[7:0]};  // Bit_Extender bit_extender_3
  assign bit_extender_4_out = {{16{1'b0}}, data_in[15:0]};  // Bit_Extender bit_extender_4
endmodule

module forwarding_unit (
  input  [31:0] wb_data,
  input  [31:0] ma_data,
  input  [4:0] rs1,
  input  [4:0] wb_rd,
  input  [4:0] ma_rd,
  input  [4:0] rs2,
  input  wb_rf_we,
  input  ma_rf_we,
  output [31:0] a,
  output [31:0] b,
  output fwA,
  output fwB
);

  wire and_1_out, and_2_out, and_3_out, and_4_out, forwarding_cmp_1_fwd, forwarding_cmp_2_fwd,
       forwarding_cmp_3_fwd, forwarding_cmp_4_fwd;

  forwarding_cmp forwarding_cmp_1 (.fwd(forwarding_cmp_1_fwd), .rd(rs1), .rs(wb_rd));
  forwarding_cmp forwarding_cmp_2 (.fwd(forwarding_cmp_2_fwd), .rd(ma_rd), .rs(rs1));
  forwarding_cmp forwarding_cmp_3 (.fwd(forwarding_cmp_3_fwd), .rd(wb_rd), .rs(rs2));
  forwarding_cmp forwarding_cmp_4 (.fwd(forwarding_cmp_4_fwd), .rd(ma_rd), .rs(rs2));
  Multiplexer #(.width(32)) multiplexer_1 (.in0(wb_data), .in1(ma_data), .out(a), .sel(and_2_out));
  Multiplexer #(.width(32)) multiplexer_2 (.in0(wb_data), .in1(ma_data), .out(b), .sel(and_4_out));
  and and_1 (and_1_out, wb_rf_we, forwarding_cmp_1_fwd);
  and and_2 (and_2_out, ma_rf_we, forwarding_cmp_2_fwd);
  and and_3 (and_3_out, wb_rf_we, forwarding_cmp_3_fwd);
  and and_4 (and_4_out, ma_rf_we, forwarding_cmp_4_fwd);
  or or_1 (fwA, and_1_out, and_2_out);
  or or_2 (fwB, and_3_out, and_4_out);
endmodule

module forwarding_cmp (
  input  [4:0] rd,
  input  [4:0] rs,
  output fwd
);

  wire comparator_1_eq, comparator_2_eq;

  Comparator #(.mode("unsigned"), .width(5)) comparator_1 (.a(rd), .b(rs), .eq(comparator_1_eq));  // open: gt, lt
  and and_1 (fwd, comparator_1_eq, ~comparator_2_eq);  // AND_Gate
  Comparator #(.mode("unsigned"), .width(5)) comparator_2 (
    .a(rd), .b({5{1'b0}}), .eq(comparator_2_eq));  // open: gt, lt
endmodule

module hold_unit (
  input  hld,
  input  ma,
  input  rst,
  input  clk,
  output hlda,
  output cclk
);

  wire and_1_out, not_1_out, or_1_out;

  and and_1 (and_1_out, hld, ~ma);  // AND_Gate
  not not_1 (not_1_out, hld);
  D_Flip_Flop d_ff_1 (.Q(hlda), .preset(and_1_out), .reset(or_1_out));  // open: D, clk, Qn
  or or_1 (or_1_out, not_1_out, rst);
  and and_2 (cclk, ~hlda, clk);  // AND_Gate
endmodule

module nop_pull (
  input  [31:0] instr_in,
  input  nop,
  output [31:0] instr_out
);

  wire not_1_out;

  Pull_Resistor pull_resistor_1 (.node(instr_out[31]));
  Pull_Resistor pull_resistor_2 (.node(instr_out[30]));
  Pull_Resistor pull_resistor_3 (.node(instr_out[29]));
  Pull_Resistor pull_resistor_4 (.node(instr_out[28]));
  Pull_Resistor pull_resistor_5 (.node(instr_out[27]));
  Pull_Resistor pull_resistor_6 (.node(instr_out[26]));
  Pull_Resistor pull_resistor_7 (.node(instr_out[25]));
  Pull_Resistor pull_resistor_8 (.node(instr_out[24]));
  Pull_Resistor pull_resistor_9 (.node(instr_out[23]));
  Pull_Resistor pull_resistor_10 (.node(instr_out[22]));
  Pull_Resistor pull_resistor_11 (.node(instr_out[21]));
  Pull_Resistor pull_resistor_12 (.node(instr_out[20]));
  Pull_Resistor pull_resistor_13 (.node(instr_out[19]));
  Pull_Resistor pull_resistor_14 (.node(instr_out[18]));
  Pull_Resistor pull_resistor_15 (.node(instr_out[17]));
  Pull_Resistor pull_resistor_16 (.node(instr_out[16]));
  assign instr_out = not_1_out ? instr_in : 32'bz;  // Controlled_Buffer controlled_buffer_1
  not not_1 (not_1_out, nop);
  Pull_Resistor pull_resistor_17 (.node(instr_out[15]));
  Pull_Resistor pull_resistor_18 (.node(instr_out[14]));
  Pull_Resistor pull_resistor_19 (.node(instr_out[13]));
  Pull_Resistor pull_resistor_20 (.node(instr_out[12]));
  Pull_Resistor pull_resistor_21 (.node(instr_out[11]));
  Pull_Resistor pull_resistor_22 (.node(instr_out[10]));
  Pull_Resistor pull_resistor_23 (.node(instr_out[9]));
  Pull_Resistor pull_resistor_24 (.node(instr_out[8]));
  Pull_Resistor pull_resistor_25 (.node(instr_out[7]));
  Pull_Resistor pull_resistor_26 (.node(instr_out[6]));
  Pull_Resistor pull_resistor_27 (.node(instr_out[5]));
  Pull_Resistor #(.pull(1)) pull_resistor_28 (.node(instr_out[4]));
  Pull_Resistor #(.pull(1)) pull_resistor_29 (.node(instr_out[1]));
  Pull_Resistor #(.pull(1)) pull_resistor_30 (.node(instr_out[0]));
  Pull_Resistor pull_resistor_31 (.node(instr_out[3]));
  Pull_Resistor pull_resistor_32 (.node(instr_out[2]));
endmodule
