// Logisim project via.circ as structural Verilog: 6 circuits, main circuit via
module via (
  input  [31:0] DataIn,
  input  [7:0] PAI,
  input  [7:0] PBI,
  input  [7:0] PCI,
  input  En,
  input  RW,
  input  [31:0] Rs,
  input  CLK,
  input  RST,
  output [7:0] PAO,
  output [7:0] PBO,
  output [7:0] PCO,
  output [31:0] DataOut
);

  wire and_1_out, and_2_out, and_3_out, decoder_1_out0, decoder_1_out2, decoder_1_out4, decoder_1_out6,
       decoder_1_out7, not_1_out, timer_8b_1_pc7, timer_8b_1_pc7en;
  wire [2:0] bit_extender_2_out;
  wire [7:0] bit_extender_1_out, io_port_1_opxi, io_port_2_opxi, io_port_3_opxi, io_port_3_pxo,
       multiplexer_1_out, pc7_ctrl_1_pci, timer_8b_1_otval, timer_8b_1_txp;
  wire [31:0] bit_extender_3_out;

  and and_1 (and_1_out, En, RW);
  and and_2 (and_2_out, En, ~RW);  // AND_Gate
  not not_1 (not_1_out, CLK);
  Bit_Extender #(.in_width(32), .out_width(8), .\type ("zero")) bit_extender_1 (.in(DataIn), .out(bit_extender_1_out));
  Decoder #(.select(3)) decoder_1 (
    .out0(decoder_1_out0), .out2(decoder_1_out2), .out4(decoder_1_out4), .out6(decoder_1_out6),
    .out7(decoder_1_out7), .sel(bit_extender_2_out), .en(and_1_out));  // open: out1, out3, out5
  Bit_Extender #(.in_width(32), .out_width(3), .\type ("zero")) bit_extender_2 (.in(Rs), .out(bit_extender_2_out));
  io_port io_port_1 (
    .WE(decoder_1_out0), .CLK(not_1_out), .RST(RST), .DataIn(bit_extender_1_out), .iPXI(PAI), .PXO(PAO),
    .oPXI(io_port_1_opxi));
  io_port io_port_2 (
    .WE(decoder_1_out2), .CLK(not_1_out), .RST(RST), .DataIn(bit_extender_1_out), .iPXI(PBI), .PXO(PBO),
    .oPXI(io_port_2_opxi));
  io_port io_port_3 (
    .WE(decoder_1_out4), .CLK(not_1_out), .RST(RST), .DataIn(bit_extender_1_out), .iPXI(pc7_ctrl_1_pci),
    .PXO(io_port_3_pxo), .oPXI(io_port_3_opxi));
  timer_8b timer_8b_1 (
    .iTVal(bit_extender_1_out), .TValEn(decoder_1_out6), .ClrTXP(and_3_out), .TCtrlEn(decoder_1_out7),
    .CLK(not_1_out), .RST(RST), .oTVal(timer_8b_1_otval), .TXP(timer_8b_1_txp), .PC7En(timer_8b_1_pc7en),
    .PC7(timer_8b_1_pc7));
  and and_3 (and_3_out, and_2_out, bit_extender_2_out[2], ~bit_extender_2_out[1], bit_extender_2_out[0]);  // AND_Gate
  Multiplexer #(.select(3), .width(8)) multiplexer_1 (
    .in0(PAO), .in1(io_port_1_opxi), .in2(PBO), .in3(io_port_2_opxi), .in4(io_port_3_pxo),
    .in5(io_port_3_opxi), .in6(timer_8b_1_otval), .in7(timer_8b_1_txp), .out(multiplexer_1_out),
    .sel(bit_extender_2_out));
  pc7_ctrl pc7_ctrl_1 (
    .Bit7(timer_8b_1_pc7), .Bit7En(timer_8b_1_pc7en), .iPCO(io_port_3_pxo), .iPCI(PCI), .PCO(PCO),
    .PCI(pc7_ctrl_1_pci));
  assign bit_extender_3_out = {{24{1'b0}}, multiplexer_1_out};  // Bit_Extender bit_extender_3
  assign DataOut = and_2_out ? bit_extender_3_out : 32'bz;  // Controlled_Buffer controlled_buffer_1
endmodule

module io_port (
  input  [7:0] DataIn,
  input  WE,
  input  CLK,
  input  RST,
  input  [7:0] iPXI,
  output [7:0] PXO,
  output [7:0] oPXI
);

  Register register_1 (.D(DataIn), .en(WE), .Q(PXO), .clk(CLK), .clr(RST));

  assign oPXI = iPXI;
endmodule

module buff8 (
  input  [7:0] DataIn,
  input  [7:0] En,
  output [7:0] DataOut
);

  assign DataOut[0] = En[0] ? DataIn[0] : 1'bz;  // Controlled_Buffer controlled_buffer_1
  assign DataOut[1] = En[1] ? DataIn[1] : 1'bz;  // Controlled_Buffer controlled_buffer_2
  assign DataOut[2] = En[2] ? DataIn[2] : 1'bz;  // Controlled_Buffer controlled_buffer_3
  assign DataOut[3] = En[3] ? DataIn[3] : 1'bz;  // Controlled_Buffer controlled_buffer_4
  assign DataOut[4] = En[4] ? DataIn[4] : 1'bz;  // Controlled_Buffer controlled_buffer_5
  assign DataOut[5] = En[5] ? DataIn[5] : 1'bz;  // Controlled_Buffer controlled_buffer_6
  assign DataOut[6] = En[6] ? DataIn[6] : 1'bz;  // Controlled_Buffer controlled_buffer_7
  assign DataOut[7] = En[7] ? DataIn[7] : 1'bz;  // Controlled_Buffer controlled_buffer_8
endmodule

module timer_8b (
  input  [7:0] iTVal,
  input  TValEn,
  input  ClrTXP,
  input  TCtrlEn,
  input  CLK,
  input  RST,
  output [7:0] oTVal,
  output [7:0] TXP,
  output PC7En,
  output PC7
);

  wire and_1_out, and_2_out, and_3_out, and_4_out, clk_divider_1_clkout, comparator_1_eq, counter_1_carry,
       d_ff_1_q, or_1_out, or_2_out, or_3_out;
  wire [7:0] register_1_q, register_2_q;

  Register #(.trigger("falling")) register_1 (
    .D(iTVal), .en(TCtrlEn), .Q({register_1_q[7:5], PC7En, register_1_q[3:0]}), .clk(CLK), .clr(RST));
  Register register_2 (.D(iTVal), .en(TValEn), .Q(register_2_q), .clk(CLK), .clr(RST));
  or or_1 (or_1_out, TValEn, and_1_out);
  Counter #(.ongoal("continue"), .trigger("falling")) counter_1 (
    .load(or_1_out), .D(register_2_q), .count(register_1_q[0]), .Q(oTVal), .carry(counter_1_carry),
    .up(1'b0), .clk(clk_divider_1_clkout), .clr(RST));
  clk_divider clk_divider_1 (
    .En(register_1_q[0]), .CLKIn(CLK), .RST(RST), .DivSel(register_1_q[3:2]), .CLKOut(clk_divider_1_clkout));
  and and_1 (and_1_out, counter_1_carry, register_1_q[1]);
  Comparator #(.mode("unsigned")) comparator_1 (.a(register_2_q), .b(oTVal), .eq(comparator_1_eq));  // open: gt, lt
  and and_2 (and_2_out, ~register_1_q[1], comparator_1_eq);  // AND_Gate
  or or_2 (or_2_out, and_2_out, and_1_out);
  and and_3 (and_3_out, counter_1_carry, register_1_q[0]);
  D_Flip_Flop d_ff_1 (.Q(d_ff_1_q), .preset(and_3_out), .reset(or_3_out));  // open: D, clk, Qn
  or or_3 (or_3_out, TValEn, RST, ClrTXP);
  T_Flip_Flop t_ff_1 (.T(PC7En), .clk(and_4_out), .Q(PC7), .reset(RST));  // open: Qn, preset
  and and_4 (and_4_out, or_2_out, register_1_q[0]);
  assign TXP = {{7{1'b0}}, d_ff_1_q};  // Bit_Extender bit_extender_1
endmodule

module pc7_ctrl (
  input  [7:0] iPCO,
  input  Bit7,
  input  Bit7En,
  input  [7:0] iPCI,
  output [7:0] PCO,
  output [7:0] PCI
);

  Multiplexer multiplexer_1 (.in0(iPCO[7]), .in1(Bit7), .out(PCO[7]), .sel(Bit7En));
  Multiplexer multiplexer_2 (.in0(iPCI[7]), .in1(1'b0), .out(PCI[7]), .sel(Bit7En));

  assign PCI[6:0] = iPCI[6:0];
  assign PCO[6:0] = iPCO[6:0];
endmodule

module clk_divider (
  input  En,
  input  CLKIn,
  input  RST,
  input  [1:0] DivSel,
  output CLKOut
);

  wire DIV2_q, DIV2_qn, DIV4_q, DIV4_qn, DIV8_q, DIV8_qn, DIV16_q;

  T_Flip_Flop DIV2 (.T(En), .clk(CLKIn), .Q(DIV2_q), .Qn(DIV2_qn), .reset(RST));  // open: preset
  T_Flip_Flop DIV4 (.T(En), .clk(DIV2_qn), .Q(DIV4_q), .Qn(DIV4_qn), .reset(RST));  // open: preset
  T_Flip_Flop DIV8 (.T(En), .clk(DIV4_qn), .Q(DIV8_q), .Qn(DIV8_qn), .reset(RST));  // open: preset
  T_Flip_Flop DIV16 (.T(En), .clk(DIV8_qn), .Q(DIV16_q), .reset(RST));  // open: Qn, preset
  Multiplexer #(.select(2)) multiplexer_1 (
    .in0(DIV2_q), .in1(DIV4_q), .in2(DIV8_q), .in3(DIV16_q), .out(CLKOut), .sel(DivSel));
endmodule
