// Logisim project simple-riscv-v-machine-128MB.circ as structural Verilog: 9 circuits, main circuit main
module main (
  input  Run_Stop
);

  wire and_1_out, button_1_out, clock_1_out, cpu_1_rd, cpu_1_wr, keyboard_1_avail,
       keyboard_interface_1_clear, keyboard_interface_1_rd_en, mem_io_1_io, mem_io_1_mem,
       terminal_interface_1_clear, terminal_interface_1_wr;
  wire [1:0] cpu_1_data_type;
  wire [3:0] cpu_1_cur_instr, cpu_1_cur_instr_2, cpu_1_cur_instr_3, cpu_1_cur_instr_4, cpu_1_cur_instr_5,
       cpu_1_cur_instr_6, cpu_1_cur_instr_7, cpu_1_cur_instr_8;
  wire [6:0] keyboard_1_data, terminal_interface_1_char;
  wire [31:0] cpu_1_addr, cpu_1_data_out, cpu_1_pc, io_interface_1_porta_out, io_interface_1_portb_out,
       io_interface_1_portc_out, io_interface_1_portd_out, keyboard_interface_1_data_out, memory_1_data_out,
       memory_1_instr, undriven, undriven_2, undriven_3;

  // LedBar #(.inputtype("row"), .matrixcols(32)) ledbar_1: pin names not known
  // LedBar #(.inputtype("row"), .matrixcols(32)) ledbar_2: pin names not known
  // LedBar #(.inputtype("row"), .matrixcols(32)) ledbar_3: pin names not known
  Hex_Digit_Display hex_digit_display_1 (.value(cpu_1_cur_instr_8));  // open: dp
  // LedBar #(.inputtype("row"), .matrixcols(32)) ledbar_4: pin names not known
  Hex_Digit_Display hex_digit_display_2 (.value(cpu_1_cur_instr_7));  // open: dp
  Hex_Digit_Display hex_digit_display_3 (.value(cpu_1_cur_instr_6));  // open: dp
  Hex_Digit_Display hex_digit_display_4 (.value(cpu_1_cur_instr_5));  // open: dp
  Hex_Digit_Display hex_digit_display_5 (.value(cpu_1_cur_instr_4));  // open: dp
  // Probe on io_interface_1_porta_out
  Hex_Digit_Display hex_digit_display_6 (.value(cpu_1_cur_instr_3));  // open: dp
  Hex_Digit_Display hex_digit_display_7 (.value(cpu_1_cur_instr_2));  // open: dp
  // Probe on undriven
  mem_io mem_io_1 (.io(mem_io_1_io), .mem(mem_io_1_mem), .addr(cpu_1_addr));
  memory memory_1 (
    .instr(memory_1_instr), .data_out(memory_1_data_out), .clk(and_1_out), .en(mem_io_1_mem),
    .data_type(cpu_1_data_type), .wr(cpu_1_wr), .rd(cpu_1_rd), .pc(cpu_1_pc), .addr(cpu_1_addr),
    .data_in(cpu_1_data_out));
  Pull_Resistor pull_resistor_1 (.node(memory_1_data_out));
  Hex_Digit_Display hex_digit_display_8 (.value(cpu_1_cur_instr));  // open: dp
  // Probe on io_interface_1_portb_out
  io_interface io_interface_1 (
    .portA_out(io_interface_1_porta_out), .portB_out(io_interface_1_portb_out),
    .portC_out(io_interface_1_portc_out), .portD_out(io_interface_1_portd_out),
    .cdata_out(memory_1_data_out), .wr(cpu_1_wr), .cs(mem_io_1_io), .rd(cpu_1_rd), .clk(and_1_out),
    .reset(button_1_out), .cdata_in(cpu_1_data_out), .a01(cpu_1_addr), .portA_in(undriven),
    .portB_in(undriven_2), .portCin(keyboard_interface_1_data_out), .portD_in(undriven_3));
  cpu cpu_1 (
    .cur_instr({cpu_1_cur_instr_8, cpu_1_cur_instr_7, cpu_1_cur_instr_6, cpu_1_cur_instr_5, cpu_1_cur_instr_4, cpu_1_cur_instr_3, cpu_1_cur_instr_2, cpu_1_cur_instr}),
    .addr(cpu_1_addr), .rd(cpu_1_rd), .wr(cpu_1_wr), .data_type(cpu_1_data_type), .pc(cpu_1_pc),
    .data_out(cpu_1_data_out), .instr(memory_1_instr), .reset(button_1_out), .clk(and_1_out),
    .data_in(memory_1_data_out));
  Clock clock_1 (.out(clock_1_out));
  Button button_1 (.out(button_1_out));
  // Probe on undriven_2
  and and_1 (and_1_out, Run_Stop, clock_1_out);
  // Probe on io_interface_1_portc_out
  // Probe on keyboard_interface_1_data_out
  TTY #(.cols(48), .rows(13)) tty_1 (
    .data(terminal_interface_1_char), .clk(and_1_out), .we(terminal_interface_1_wr),
    .clr(terminal_interface_1_clear));
  terminal_interface terminal_interface_1 (
    .char(terminal_interface_1_char), .wr(terminal_interface_1_wr), .clear(terminal_interface_1_clear),
    .cmd(io_interface_1_porta_out), .clear_in(button_1_out));
  sounder sounder_1 (.clear(button_1_out), .cmd(io_interface_1_portb_out));  // open: freq, en, vol
  Keyboard keyboard_1 (
    .clk(and_1_out), .re(keyboard_interface_1_rd_en), .clr(keyboard_interface_1_clear),
    .avail(keyboard_1_avail), .data(keyboard_1_data));
  keyboard_interface keyboard_interface_1 (
    .data_out(keyboard_interface_1_data_out), .rd_en(keyboard_interface_1_rd_en),
    .clear(keyboard_interface_1_clear), .char_valid(keyboard_1_avail), .clear_in(button_1_out),
    .cmd(io_interface_1_portc_out), .kb_char(keyboard_1_data));
  // Buzzer buzzer_1: pin names not known
  // Probe on io_interface_1_portd_out
  // Probe on undriven_3

  // Notes on the sheet:
  //   Data Bus
  //   Address Bus
  //   Current Instruction
  //   Port A
  //   Clock
  //   Reset
  //   Port B
  //   Port C
  //   Port D
endmodule

module cpu (
  input  [31:0] data_in,
  input  reset,
  input  clk,
  input  [31:0] instr,
  output [31:0] data_out,
  output [1:0] data_type,
  output rd,
  output wr,
  output [31:0] addr,
  output [31:0] pc,
  output [31:0] cur_instr
);

  wire comparator_1_eq, comparator_1_gt, comparator_1_lt, comparator_2_gt, comparator_2_lt,
       decode_control_1_alu_a, decode_control_1_pc_ld, decode_control_1_rf_we, not_1_out, or_1_out, or_3_out,
       or_4_out;
  wire [0:0] and_1_out;
  wire [1:0] decode_control_1_alu_b, decode_control_1_pc_src, decode_control_1_rf_src;
  wire [4:0] decode_control_1_rd, decode_control_1_rs1, decode_control_1_rs2, pla_1_out;
  wire [6:0] decode_control_1_alu_op;
  wire [6:1] decode_control_1_func7;
  wire [31:0] adder_1_out, adder_2_out, adder_3_out, adder_4_out, and_2_out, bit_extender_5_out,
       bit_extender_6_out, bit_extender_7_out, bit_extender_8_out, bit_extender_15_out, bit_extender_16_out,
       bit_extender_17_out, bit_extender_18_out, bit_extender_19_out, bit_extender_20_out,
       decode_control_1_imm, decoder_1_out0, divider_1_out, divider_1_rem, divider_2_out, divider_2_rem,
       multiplexer_1_out, multiplexer_2_out, multiplexer_3_out, multiplexer_4_out, multiplexer_5_out,
       multiplexer_6_out, multiplier_1_out, or_2_out, register_2_q, register_3_q, register_4_q, register_5_q,
       register_6_q, register_7_q, register_8_q, register_9_q, register_10_q, register_11_q, register_12_q,
       register_13_q, register_14_q, register_15_q, register_16_q, register_17_q, register_18_q,
       register_19_q, register_20_q, register_21_q, register_22_q, register_23_q, register_24_q,
       register_25_q, register_26_q, register_27_q, register_28_q, register_29_q, register_30_q,
       register_31_q, register_32_q, shifter_1_out, shifter_2_out, shifter_3_out, subtractor_1_out, xor_1_out;
  wire [31:11] bit_extender_3_out, bit_extender_4_out;
  wire [31:12] bit_extender_2_out;
  wire [31:20] bit_extender_1_out;
  wire [63:0] bit_extender_9_out, bit_extender_10_out, bit_extender_11_out, bit_extender_12_out,
       bit_extender_13_out, bit_extender_14_out, multiplier_2_out, multiplier_3_out, multiplier_4_out;

  assign bit_extender_1_out = {{11{decode_control_1_imm[31]}}, decode_control_1_imm[31]};  // Bit_Extender bit_extender_1
  assign bit_extender_2_out = {{19{decode_control_1_imm[31]}}, decode_control_1_imm[31]};  // Bit_Extender bit_extender_2
  assign bit_extender_3_out = {{20{decode_control_1_imm[31]}}, decode_control_1_imm[31]};  // Bit_Extender bit_extender_3
  assign bit_extender_4_out = {{20{decode_control_1_imm[31]}}, decode_control_1_imm[31]};  // Bit_Extender bit_extender_4
  Multiplexer #(.select(3), .width(32)) multiplexer_1 (
    .in0(bit_extender_5_out), .in1(bit_extender_6_out), .in2(data_in), .in3({32{1'b0}}),
    .in4(bit_extender_7_out), .in5(bit_extender_8_out), .in6({32{1'b0}}), .in7({32{1'b0}}),
    .out(multiplexer_1_out));  // open: sel
  or or_1 (or_1_out, addr[0], decode_control_1_pc_src[1]);
  assign bit_extender_5_out = {{24{data_in[7]}}, data_in[7:0]};  // Bit_Extender bit_extender_5
  assign bit_extender_6_out = {{16{data_in[15]}}, data_in[15:0]};  // Bit_Extender bit_extender_6
  assign bit_extender_7_out = {{24{1'b0}}, data_in[7:0]};  // Bit_Extender bit_extender_7
  assign bit_extender_8_out = {{16{1'b0}}, data_in[15:0]};  // Bit_Extender bit_extender_8
  Multiplexer #(.select(2), .width(32)) multiplexer_2 (
    .in0(multiplexer_1_out), .in1(adder_1_out), .in2(addr), .in3({decode_control_1_imm[31:12], {12{1'b0}}}),
    .out(multiplexer_2_out), .sel(decode_control_1_rf_src));
  Adder #(.width(32)) adder_1 (.a(pc), .b(32'h4), .out(adder_1_out));  // open: cin, cout
  Adder #(.width(32)) adder_2 (
    .a(pc),
    .b({bit_extender_2_out, decode_control_1_imm[7], decode_control_1_imm[30:25], decode_control_1_imm[11:8], 1'b0}),
    .out(adder_2_out));  // open: cin, cout
  Adder #(.width(32)) adder_3 (
    .a(pc),
    .b({bit_extender_1_out, decode_control_1_imm[19:12], decode_control_1_imm[20], decode_control_1_imm[30:21], 1'b0}),
    .out(adder_3_out));  // open: cin, cout
  and and_1 (and_1_out[0], or_1_out, decode_control_1_pc_src[0]);
  Multiplexer #(.select(5), .width(32)) multiplexer_3 (
    .in0({32{1'b0}}), .in1(register_30_q), .in2(register_27_q), .in3(register_26_q), .in4(register_24_q),
    .in5(register_22_q), .in6(register_19_q), .in7(register_18_q), .in8(register_16_q), .in9(register_14_q),
    .in10(register_11_q), .in11(register_10_q), .in12(register_8_q), .in13(register_6_q),
    .in14(register_3_q), .in15(register_2_q), .in16(register_32_q), .in17(register_31_q),
    .in18(register_29_q), .in19(register_28_q), .in20(register_25_q), .in21(register_23_q),
    .in22(register_21_q), .in23(register_20_q), .in24(register_17_q), .in25(register_15_q),
    .in26(register_13_q), .in27(register_12_q), .in28(register_9_q), .in29(register_7_q),
    .in30(register_5_q), .in31(register_4_q), .out(multiplexer_3_out), .sel(decode_control_1_rs1));
  Decoder #(.select(5)) decoder_1 (
    .out0(decoder_1_out0[0]), .out1(decoder_1_out0[1]), .out2(decoder_1_out0[2]), .out3(decoder_1_out0[3]),
    .out4(decoder_1_out0[4]), .out5(decoder_1_out0[5]), .out6(decoder_1_out0[6]), .out7(decoder_1_out0[7]),
    .out8(decoder_1_out0[8]), .out9(decoder_1_out0[9]), .out10(decoder_1_out0[10]),
    .out11(decoder_1_out0[11]), .out12(decoder_1_out0[12]), .out13(decoder_1_out0[13]),
    .out14(decoder_1_out0[14]), .out15(decoder_1_out0[15]), .out16(decoder_1_out0[16]),
    .out17(decoder_1_out0[17]), .out18(decoder_1_out0[18]), .out19(decoder_1_out0[19]),
    .out20(decoder_1_out0[20]), .out21(decoder_1_out0[21]), .out22(decoder_1_out0[22]),
    .out23(decoder_1_out0[23]), .out24(decoder_1_out0[24]), .out25(decoder_1_out0[25]),
    .out26(decoder_1_out0[26]), .out27(decoder_1_out0[27]), .out28(decoder_1_out0[28]),
    .out29(decoder_1_out0[29]), .out30(decoder_1_out0[30]), .out31(decoder_1_out0[31]),
    .sel(decode_control_1_rd), .en(decode_control_1_rf_we));
  Multiplexer #(.select(2), .width(32)) multiplexer_4 (
    .in0(adder_1_out), .in1(adder_2_out), .in2(adder_3_out), .in3({addr[31:1], 1'b0}),
    .out(multiplexer_4_out), .sel({decode_control_1_pc_src[1], and_1_out[0]}));
  Register #(.width(32)) register_1 (
    .D(multiplexer_4_out), .en(decode_control_1_pc_ld), .Q(pc), .clk(clk), .clr(reset));
  Register #(.width(32)) register_2 (
    .D(multiplexer_2_out), .en(decoder_1_out0[15]), .Q(register_2_q), .clk(clk), .clr(reset));
  Register #(.width(32)) register_3 (
    .D(multiplexer_2_out), .en(decoder_1_out0[14]), .Q(register_3_q), .clk(clk), .clr(reset));
  Register #(.width(32)) register_4 (
    .D(multiplexer_2_out), .en(decoder_1_out0[31]), .Q(register_4_q), .clk(clk), .clr(reset));
  Register #(.width(32)) register_5 (
    .D(multiplexer_2_out), .en(decoder_1_out0[30]), .Q(register_5_q), .clk(clk), .clr(reset));
  Register #(.width(32)) register_6 (
    .D(multiplexer_2_out), .en(decoder_1_out0[13]), .Q(register_6_q), .clk(clk), .clr(reset));
  Register #(.width(32)) register_7 (
    .D(multiplexer_2_out), .en(decoder_1_out0[29]), .Q(register_7_q), .clk(clk), .clr(reset));
  decode_control decode_control_1 (
    .cur_instr(cur_instr), .rf_src(decode_control_1_rf_src), .rf_we(decode_control_1_rf_we),
    .alu_op(decode_control_1_alu_op[1:0]), .alu_a(decode_control_1_alu_a), .alu_b(decode_control_1_alu_b),
    .mem_wr(wr), .mem_rd(rd), .rd(decode_control_1_rd), .func3({decode_control_1_alu_op[4], data_type}),
    .rs1(decode_control_1_rs1), .rs2(decode_control_1_rs2),
    .func7({decode_control_1_func7[6], decode_control_1_alu_op[6], decode_control_1_func7[4:1], decode_control_1_alu_op[5]}),
    .imm(decode_control_1_imm), .pc_ld(decode_control_1_pc_ld), .pc_src(decode_control_1_pc_src), .clk(clk),
    .reset(reset), .instr(instr));
  Register #(.width(32)) register_8 (
    .D(multiplexer_2_out), .en(decoder_1_out0[12]), .Q(register_8_q), .clk(clk), .clr(reset));
  Register #(.width(32)) register_9 (
    .D(multiplexer_2_out), .en(decoder_1_out0[28]), .Q(register_9_q), .clk(clk), .clr(reset));
  Register #(.width(32)) register_10 (
    .D(multiplexer_2_out), .en(decoder_1_out0[11]), .Q(register_10_q), .clk(clk), .clr(reset));
  Register #(.width(32)) register_11 (
    .D(multiplexer_2_out), .en(decoder_1_out0[10]), .Q(register_11_q), .clk(clk), .clr(reset));
  Register #(.width(32)) register_12 (
    .D(multiplexer_2_out), .en(decoder_1_out0[27]), .Q(register_12_q), .clk(clk), .clr(reset));
  Register #(.width(32)) register_13 (
    .D(multiplexer_2_out), .en(decoder_1_out0[26]), .Q(register_13_q), .clk(clk), .clr(reset));
  Register #(.width(32)) register_14 (
    .D(multiplexer_2_out), .en(decoder_1_out0[9]), .Q(register_14_q), .clk(clk), .clr(reset));
  Register #(.width(32)) register_15 (
    .D(multiplexer_2_out), .en(decoder_1_out0[25]), .Q(register_15_q), .clk(clk), .clr(reset));
  Register #(.width(32)) register_16 (
    .D(multiplexer_2_out), .en(decoder_1_out0[8]), .Q(register_16_q), .clk(clk), .clr(reset));
  Register #(.width(32)) register_17 (
    .D(multiplexer_2_out), .en(decoder_1_out0[24]), .Q(register_17_q), .clk(clk), .clr(reset));
  Register #(.width(32)) register_18 (
    .D(multiplexer_2_out), .en(decoder_1_out0[7]), .Q(register_18_q), .clk(clk), .clr(reset));
  Register #(.width(32)) register_19 (
    .D(multiplexer_2_out), .en(decoder_1_out0[6]), .Q(register_19_q), .clk(clk), .clr(reset));
  Register #(.width(32)) register_20 (
    .D(multiplexer_2_out), .en(decoder_1_out0[23]), .Q(register_20_q), .clk(clk), .clr(reset));
  Register #(.width(32)) register_21 (
    .D(multiplexer_2_out), .en(decoder_1_out0[22]), .Q(register_21_q), .clk(clk), .clr(reset));
  Register #(.width(32)) register_22 (
    .D(multiplexer_2_out), .en(decoder_1_out0[5]), .Q(register_22_q), .clk(clk), .clr(reset));
  Register #(.width(32)) register_23 (
    .D(multiplexer_2_out), .en(decoder_1_out0[21]), .Q(register_23_q), .clk(clk), .clr(reset));
  Register #(.width(32)) register_24 (
    .D(multiplexer_2_out), .en(decoder_1_out0[4]), .Q(register_24_q), .clk(clk), .clr(reset));
  Register #(.width(32)) register_25 (
    .D(multiplexer_2_out), .en(decoder_1_out0[20]), .Q(register_25_q), .clk(clk), .clr(reset));
  assign bit_extender_9_out = {{32{multiplexer_5_out[31]}}, multiplexer_5_out};  // Bit_Extender bit_extender_9
  assign bit_extender_10_out = {{32{multiplexer_6_out[31]}}, multiplexer_6_out};  // Bit_Extender bit_extender_10
  assign bit_extender_11_out = {{32{1'b0}}, multiplexer_5_out};  // Bit_Extender bit_extender_11
  assign bit_extender_12_out = {{32{1'b0}}, multiplexer_6_out};  // Bit_Extender bit_extender_12
  assign bit_extender_13_out = {{32{multiplexer_5_out[31]}}, multiplexer_5_out};  // Bit_Extender bit_extender_13
  assign bit_extender_14_out = {{32{1'b0}}, multiplexer_6_out};  // Bit_Extender bit_extender_14
  Register #(.width(32)) register_26 (
    .D(multiplexer_2_out), .en(decoder_1_out0[3]), .Q(register_26_q), .clk(clk), .clr(reset));
  Register #(.width(32)) register_27 (
    .D(multiplexer_2_out), .en(decoder_1_out0[2]), .Q(register_27_q), .clk(clk), .clr(reset));
  Register #(.width(32)) register_28 (
    .D(multiplexer_2_out), .en(decoder_1_out0[19]), .Q(register_28_q), .clk(clk), .clr(reset));
  Register #(.width(32)) register_29 (
    .D(multiplexer_2_out), .en(decoder_1_out0[18]), .Q(register_29_q), .clk(clk), .clr(reset));
  Adder #(.width(32)) adder_4 (.a(multiplexer_5_out), .b(multiplexer_6_out), .out(adder_4_out));  // open: cin, cout
  Subtractor #(.width(32)) subtractor_1 (
    .a(multiplexer_5_out), .b(multiplexer_6_out), .out(subtractor_1_out));  // open: bin, bout
  Multiplier #(.width(32)) multiplier_1 (
    .a(multiplexer_5_out), .b(multiplexer_6_out), .out(multiplier_1_out));  // open: cin, cout
  Multiplier #(.width(64)) multiplier_2 (
    .a(bit_extender_9_out), .b(bit_extender_10_out), .out(multiplier_2_out));  // open: cin, cout
  Multiplier #(.width(64)) multiplier_3 (
    .a(bit_extender_11_out), .b(bit_extender_12_out), .out(multiplier_3_out));  // open: cin, cout
  Multiplier #(.width(64)) multiplier_4 (
    .a(bit_extender_13_out), .b(bit_extender_14_out), .out(multiplier_4_out));  // open: cin, cout
  Divider #(.mode("twosComplement"), .width(32)) divider_1 (
    .a(multiplexer_5_out), .b(multiplexer_6_out), .out(divider_1_out), .rem(divider_1_rem));  // open: upper
  Divider #(.width(32)) divider_2 (
    .a(multiplexer_5_out), .b(multiplexer_6_out), .out(divider_2_out), .rem(divider_2_rem));  // open: upper
  Comparator #(.width(32)) comparator_1 (
    .a(multiplexer_5_out), .b(multiplexer_6_out), .gt(comparator_1_gt), .eq(comparator_1_eq),
    .lt(comparator_1_lt));
  Comparator #(.mode("unsigned"), .width(32)) comparator_2 (
    .a(multiplexer_5_out), .b(multiplexer_6_out), .gt(comparator_2_gt), .lt(comparator_2_lt));  // open: eq
  assign and_2_out = multiplexer_5_out & multiplexer_6_out;  // AND_Gate and_2, 32 bits wide
  assign or_2_out = multiplexer_5_out | multiplexer_6_out;  // OR_Gate or_2, 32 bits wide
  assign xor_1_out = multiplexer_5_out ^ multiplexer_6_out;  // XOR_Gate xor_1, 32 bits wide
  Shifter #(.width(32)) shifter_1 (.in(multiplexer_5_out), .\dist (multiplexer_6_out[4:0]), .out(shifter_1_out));
  Shifter #(.shift("lr"), .width(32)) shifter_2 (
    .in(multiplexer_5_out), .\dist (multiplexer_6_out[4:0]), .out(shifter_2_out));
  Shifter #(.shift("ar"), .width(32)) shifter_3 (
    .in(multiplexer_5_out), .\dist (multiplexer_6_out[4:0]), .out(shifter_3_out));
  Register #(.width(32)) register_30 (
    .D(multiplexer_2_out), .en(decoder_1_out0[1]), .Q(register_30_q), .clk(clk), .clr(reset));
  Register #(.width(32)) register_31 (
    .D(multiplexer_2_out), .en(decoder_1_out0[17]), .Q(register_31_q), .clk(clk), .clr(reset));
  or or_3 (or_3_out, comparator_1_gt, comparator_1_eq);
  not not_1 (not_1_out, comparator_1_eq);
  or or_4 (or_4_out, comparator_2_gt, comparator_1_eq);
  Register #(.width(32)) register_32 (
    .D(multiplexer_2_out), .en(decoder_1_out0[16]), .Q(register_32_q), .clk(clk), .clr(reset));
  assign bit_extender_15_out = {{31{1'b0}}, or_3_out};  // Bit_Extender bit_extender_15
  assign bit_extender_16_out = {{31{1'b0}}, comparator_1_eq};  // Bit_Extender bit_extender_16
  assign bit_extender_17_out = {{31{1'b0}}, not_1_out};  // Bit_Extender bit_extender_17
  assign bit_extender_18_out = {{31{1'b0}}, comparator_1_lt};  // Bit_Extender bit_extender_18
  assign bit_extender_19_out = {{31{1'b0}}, or_4_out};  // Bit_Extender bit_extender_19
  assign bit_extender_20_out = {{31{1'b0}}, comparator_2_lt};  // Bit_Extender bit_extender_20
  Multiplexer #(.width(32)) multiplexer_5 (
    .in0(multiplexer_3_out), .in1(pc), .out(multiplexer_5_out), .sel(decode_control_1_alu_a));
  Multiplexer #(.select(2), .width(32)) multiplexer_6 (
    .in0(data_out), .in1({decode_control_1_imm[31:12], {12{1'b0}}}),
    .in2({bit_extender_3_out, decode_control_1_imm[30:20]}),
    .in3({bit_extender_4_out, decode_control_1_imm[30:25], decode_control_1_imm[11:7]}),
    .out(multiplexer_6_out), .sel(decode_control_1_alu_b));
  Multiplexer #(.select(5), .width(32)) multiplexer_7 (
    .in0(adder_4_out), .in1(subtractor_1_out), .in2(multiplier_1_out), .in3(multiplier_2_out[63:32]),
    .in4(multiplier_3_out[63:32]), .in5(multiplier_4_out[63:32]), .in6(divider_1_out), .in7(divider_1_rem),
    .in8(divider_2_out), .in9(divider_2_rem), .in10(bit_extender_15_out), .in11(bit_extender_16_out),
    .in12(bit_extender_17_out), .in13(bit_extender_18_out), .in14(bit_extender_19_out),
    .in15(bit_extender_20_out), .in16(and_2_out), .in17(or_2_out), .in18(xor_1_out), .in19(shifter_1_out),
    .in20(shifter_2_out), .in21(shifter_3_out), .in22({32{1'b0}}), .in23({32{1'b0}}), .in24({32{1'b0}}),
    .in25({32{1'b0}}), .in26({32{1'b0}}), .in27({32{1'b0}}), .in28({32{1'b0}}), .in29({32{1'b0}}),
    .in30({32{1'b0}}), .in31({32{1'b0}}), .out(addr), .sel(pla_1_out));
  PLA #(.in_width(7), .out_width(5), .\table ("xxxxx00 00000 # ADD\n0000001 00000 # R-ADD\n1000001 00001 # R-SUB\n0000101 10011 # R-SLL\n0001001 01101 # R-SLT\n0001101 01111 # R-SLTU\n0010001 10010 # R-XOR\n0010101 10100 # R-SRL\n1010101 10101 # R-SRA\n0011001 10001 # R-OR\n0011101 10000 # R-AND\nxx00010 00000 # I-ADD\nxx01010 01101 # I-SLT\nxx01110 01111 # I-SLTU\nxx10010 10010 # I-XOR\nxx11010 10001 # I-OR\nxx11110 10000 # I-AND\n0100001 00010 # R-MUL\n0100101 00011 # R-MULH\n0101001 00100 # R-MULHU\n0101101 00101 # R-MULHSU\n0110001 00110 # R-DIV\n0110101 01000 # R-DIVU\n0111001 00111 # R-REM\n0111101 01001 # R-REMU\n0x00110 10011 # I-SLL\n0x10110 10100 # I-SRL\n1x10110 10101 # I-SRA\nxx00011 01011 # B-EQ\nxx00111 01100 # B-NE\nxx10011 01101 # B-LT\nxx10111 01010 # B-GE\nxx11011 01111 # B-LTU\nxx11111 01110 # B-GEU")) pla_1 (
    .in({decode_control_1_alu_op[6:4], data_type, decode_control_1_alu_op[1:0]}), .out(pla_1_out));
  Multiplexer #(.select(5), .width(32)) multiplexer_8 (
    .in0({32{1'b0}}), .in1(register_30_q), .in2(register_27_q), .in3(register_26_q), .in4(register_24_q),
    .in5(register_22_q), .in6(register_19_q), .in7(register_18_q), .in8(register_16_q), .in9(register_14_q),
    .in10(register_11_q), .in11(register_10_q), .in12(register_8_q), .in13(register_6_q),
    .in14(register_3_q), .in15(register_2_q), .in16(register_32_q), .in17(register_31_q),
    .in18(register_29_q), .in19(register_28_q), .in20(register_25_q), .in21(register_23_q),
    .in22(register_21_q), .in23(register_20_q), .in24(register_17_q), .in25(register_15_q),
    .in26(register_13_q), .in27(register_12_q), .in28(register_9_q), .in29(register_7_q),
    .in30(register_5_q), .in31(register_4_q), .out(data_out), .sel(decode_control_1_rs2));

  // Notes on the sheet:
  //   J
  //   B
  //   U
  //   I
  //   S
  //   M1-S
endmodule

module decode_control (
  input  [31:0] instr,
  input  clk,
  input  reset,
  output pc_ld,
  output [1:0] pc_src,
  output [1:0] rf_src,
  output rf_we,
  output [1:0] alu_op,
  output alu_a,
  output [1:0] alu_b,
  output mem_wr,
  output mem_rd,
  output [4:0] rd,
  output [2:0] func3,
  output [4:0] rs1,
  output [4:0] rs2,
  output [6:0] func7,
  output [31:0] imm,
  output [31:0] cur_instr
);

  wire or_1_out;
  wire [31:0] multiplexer_1_out;

  Multiplexer #(.width(32)) multiplexer_1 (.in0(instr), .in1(32'h13), .out(multiplexer_1_out), .sel(or_1_out));
  Register #(.trigger("falling"), .width(32)) ir (
    .D(multiplexer_1_out), .Q(cur_instr), .clk(clk), .clr(reset));  // open: en
  PLA #(.in_width(7), .out_width(13), .\table ("1100011 0000011000011 # BXX\n1100111 0010000101111 # JALR\n1101111 0000000101101 # JAL\n0110111 0000000111001 # LUI\n0010111 0001100110001 # AUIPC\n0010011 0010010110001 # R-I\n0110011 0000001110001 # R-R\n0000011 1010000100000 # LOAD\n0100011 0111000000000 # STORE")) pla_1 (
    .in(cur_instr[6:0]), .out({mem_rd, mem_wr, alu_b, alu_a, alu_op, rf_we, rf_src, pc_src, pc_ld}));
  or or_1 (or_1_out, mem_wr, mem_rd);

  assign func3 = cur_instr[14:12];
  assign func7 = cur_instr[31:25];
  assign imm = {cur_instr[31:7], {7{1'b0}}};
  assign rd = cur_instr[11:7];
  assign rs1 = cur_instr[19:15];
  assign rs2 = cur_instr[24:20];

  // Notes on the sheet:
  //   nop
endmodule

module keyboard_interface (
  input  [6:0] kb_char,
  input  char_valid,
  input  [31:0] cmd,
  input  clear_in,
  output [31:0] data_out,
  output rd_en,
  output clear
);

  wire [31:0] bit_extender_1_out;

  assign bit_extender_1_out = {{24{1'b0}}, {char_valid, kb_char}};  // Bit_Extender bit_extender_1
  or or_1 (clear, cmd[1], clear_in);
  assign data_out = cmd[0] ? bit_extender_1_out : 32'bz;  // Controlled_Buffer controlled_buffer_1

  assign rd_en = cmd[0];
endmodule

module terminal_interface (
  input  [31:0] cmd,
  input  clear_in,
  output [6:0] char,
  output wr,
  output clear
);

  or or_1 (clear, cmd[8], clear_in);

  assign char = cmd[6:0];
  assign wr = cmd[7];
endmodule

module io_interface (
  input  [31:0] cdata_in,
  input  [31:0] a01,
  input  wr,
  input  cs,
  input  rd,
  input  clk,
  input  reset,
  input  [31:0] portA_in,
  input  [31:0] portB_in,
  input  [31:0] portCin,
  input  [31:0] portD_in,
  output [31:0] portA_out,
  output [31:0] portB_out,
  output [31:0] portC_out,
  output [31:0] portD_out,
  output [31:0] cdata_out
);

  wire and_1_out, and_2_out, decoder_1_out0, decoder_1_out1, decoder_1_out2, decoder_1_out3;
  wire [31:0] multiplexer_1_out, register_1_q;

  Decoder #(.select(2)) decoder_1 (
    .out0(decoder_1_out0), .out1(decoder_1_out1), .out2(decoder_1_out2), .out3(decoder_1_out3),
    .sel(a01[1:0]), .en(and_1_out));
  and and_1 (and_1_out, wr, cs);
  and and_2 (and_2_out, cs, rd);
  Multiplexer #(.disabled("Z"), .select(2), .width(32)) multiplexer_1 (
    .in0(portA_in), .in1(portB_in), .in2(portCin), .in3(portD_in), .out(multiplexer_1_out));  // open: sel
  Register #(.width(32)) register_1 (.D(multiplexer_1_out), .en(and_1_out), .Q(register_1_q), .clk(clk), .clr(reset));
  assign portA_out = decoder_1_out0 ? cdata_in : 32'bz;  // Controlled_Buffer controlled_buffer_1
  assign portB_out = decoder_1_out1 ? cdata_in : 32'bz;  // Controlled_Buffer controlled_buffer_2
  assign portC_out = decoder_1_out2 ? cdata_in : 32'bz;  // Controlled_Buffer controlled_buffer_3
  assign portD_out = decoder_1_out3 ? cdata_in : 32'bz;  // Controlled_Buffer controlled_buffer_4
  assign cdata_out = and_2_out ? register_1_q : 32'bz;  // Controlled_Buffer controlled_buffer_5
endmodule

module mem_io (
  input  [31:0] addr,
  output io,
  output mem
);

  and and_1 (io, addr[2], addr[3], addr[4], addr[5], addr[6], addr[7], addr[8], addr[9], addr[10], addr[11], addr[12], addr[13], addr[14], addr[15], addr[16], addr[17], addr[18], addr[19], addr[20], addr[21], addr[22], addr[23], addr[24], addr[25], addr[26], ~addr[27], ~addr[28], ~addr[29], ~addr[30], ~addr[31]);  // AND_Gate
  not not_1 (mem, io);

  // Notes on the sheet:
  //   7FFFFFC-7FFFFFF
endmodule

module sounder (
  input  [31:0] cmd,
  input  clear,
  output [13:0] freq,
  output en,
  output [6:0] vol
);

  Register #(.width(14)) register_1 (.D(cmd[13:0]), .Q(freq), .clk(cmd[14]), .clr(clear));  // open: en

  assign en = 1'b1;
  assign vol = {7{1'b1}};
endmodule

module memory (
  input  clk,
  input  [31:0] pc,
  input  [31:0] addr,
  input  [1:0] data_type,
  input  [31:0] data_in,
  input  en,
  input  wr,
  input  rd,
  output [31:0] instr,
  output [31:0] data_out
);

  wire and_1_out, and_2_out, demultiplexer_1_out0, demultiplexer_1_out1, demultiplexer_1_out2,
       demultiplexer_1_out3, demultiplexer_1_out4, demultiplexer_1_out5, demultiplexer_1_out6,
       demultiplexer_1_out7, or_1_out, or_2_out;
  wire [7:0] ram_2_p12, ram_2_p13, ram_2_p14, ram_2_p15, ram_3_p12, ram_3_p13, ram_3_p14, ram_3_p15,
       ram_4_p12, ram_4_p13, ram_4_p14, ram_4_p15, ram_5_p12, ram_5_p13, ram_5_p14, ram_5_p15, ram_6_p11,
       ram_6_p12, ram_6_p13, ram_6_p14, ram_7_p13, ram_7_p14, ram_7_p15, ram_7_p16, ram_8_p16, ram_8_p17,
       ram_8_p18, ram_8_p19, ram_8_p20, ram_8_p21, ram_8_p22, ram_8_p23;
  wire [31:0] demultiplexer_2_out1, multiplexer_1_out, multiplexer_2_out;

  or or_1 (or_1_out, data_type[0], data_type[1]);
  and and_1 (and_1_out, en, wr);
  and and_2 (and_2_out, en, rd);
  Multiplexer #(.width(32)) multiplexer_1 (.in0(pc), .in1(addr), .out(multiplexer_1_out), .sel(or_2_out));
  or or_2 (or_2_out, and_2_out, and_1_out);
  Demultiplexer #(.select(3)) demultiplexer_1 (
    .out0(demultiplexer_1_out0), .out1(demultiplexer_1_out1), .out2(demultiplexer_1_out2),
    .out3(demultiplexer_1_out3), .out4(demultiplexer_1_out4), .out5(demultiplexer_1_out5),
    .out6(demultiplexer_1_out6), .out7(demultiplexer_1_out7), .in(and_1_out), .sel(multiplexer_1_out[26:24]));
  // RAM #(.addrWidth(24), .enables("line"), .line("quad"), .misaligned("true"), .\type ("nonvolatile")) ram_1: pin names not known; wires that end beside it: multiplexer_1_out[23:0], demultiplexer_1_out0, 1'b1, or_1_out, data_type[1], data_type[1], clk
  // RAM #(.addrWidth(24), .enables("line"), .line("quad"), .misaligned("true"), .\type ("nonvolatile")) ram_2: pin names not known; wires that end beside it: data_in[7:0], data_in[15:8], data_in[23:16], data_in[31:24], multiplexer_1_out[23:0], demultiplexer_1_out1, 1'b1, or_1_out, data_type[1], data_type[1], clk, ram_2_p12, ram_2_p13, ram_2_p14, ram_2_p15
  // RAM #(.addrWidth(24), .enables("line"), .line("quad"), .misaligned("true"), .\type ("nonvolatile")) ram_3: pin names not known; wires that end beside it: data_in[7:0], data_in[15:8], data_in[23:16], data_in[31:24], multiplexer_1_out[23:0], demultiplexer_1_out2, 1'b1, or_1_out, data_type[1], data_type[1], clk, ram_3_p12, ram_3_p13, ram_3_p14, ram_3_p15
  // RAM #(.addrWidth(24), .enables("line"), .line("quad"), .misaligned("true"), .\type ("nonvolatile")) ram_4: pin names not known; wires that end beside it: data_in[7:0], data_in[15:8], data_in[23:16], data_in[31:24], multiplexer_1_out[23:0], demultiplexer_1_out3, 1'b1, or_1_out, data_type[1], data_type[1], clk, ram_4_p12, ram_4_p13, ram_4_p14, ram_4_p15
  // RAM #(.addrWidth(24), .enables("line"), .line("quad"), .misaligned("true"), .\type ("nonvolatile")) ram_5: pin names not known; wires that end beside it: data_in[7:0], data_in[15:8], data_in[23:16], data_in[31:24], multiplexer_1_out[23:0], demultiplexer_1_out4, 1'b1, or_1_out, data_type[1], data_type[1], clk, ram_5_p12, ram_5_p13, ram_5_p14, ram_5_p15
  // RAM #(.addrWidth(24), .enables("line"), .line("quad"), .misaligned("true"), .\type ("nonvolatile")) ram_6: pin names not known; wires that end beside it: data_in[7:0], data_in[15:8], data_in[23:16], data_in[31:24], multiplexer_1_out[23:0], demultiplexer_1_out5, 1'b1, or_1_out, data_type[1], data_type[1], ram_6_p11, ram_6_p12, ram_6_p13, ram_6_p14
  // RAM #(.addrWidth(24), .enables("line"), .line("quad"), .misaligned("true"), .\type ("nonvolatile")) ram_7: pin names not known; wires that end beside it: clk, data_in[7:0], data_in[15:8], data_in[23:16], data_in[31:24], multiplexer_1_out[23:0], demultiplexer_1_out6, 1'b1, or_1_out, data_type[1], data_type[1], clk, ram_7_p13, ram_7_p14, ram_7_p15, ram_7_p16
  // RAM #(.addrWidth(24), .enables("line"), .line("quad"), .misaligned("true"), .\type ("nonvolatile")) ram_8: pin names not known; wires that end beside it: data_in[7:0], data_in[15:8], data_in[23:16], data_in[31:24], multiplexer_1_out[23:0], demultiplexer_1_out7, 1'b1, or_1_out, data_type[1], data_type[1], clk, data_in[7:0], data_in[15:8], data_in[23:16], data_in[31:24], ram_8_p16, ram_8_p17, ram_8_p18, ram_8_p19, ram_8_p20, ram_8_p21, ram_8_p22, ram_8_p23
  Multiplexer #(.disabled("Z"), .select(3), .width(32)) multiplexer_2 (
    .in0({ram_2_p15, ram_2_p14, ram_2_p13, ram_2_p12}), .in1({ram_3_p15, ram_3_p14, ram_3_p13, ram_3_p12}),
    .in2({ram_4_p15, ram_4_p14, ram_4_p13, ram_4_p12}), .in3({ram_5_p15, ram_5_p14, ram_5_p13, ram_5_p12}),
    .in4({ram_6_p14, ram_6_p13, ram_6_p12, ram_6_p11}), .in5({ram_7_p16, ram_7_p15, ram_7_p14, ram_7_p13}),
    .in6({ram_8_p19, ram_8_p18, ram_8_p17, ram_8_p16}), .in7({ram_8_p23, ram_8_p22, ram_8_p21, ram_8_p20}),
    .out(multiplexer_2_out), .sel(multiplexer_1_out[26:24]));
  Demultiplexer #(.width(32)) demultiplexer_2 (
    .out0(instr), .out1(demultiplexer_2_out1), .in(multiplexer_2_out), .sel(or_2_out));
  assign data_out = and_2_out ? demultiplexer_2_out1 : 32'bz;  // Controlled_Buffer controlled_buffer_1
endmodule
